// Logisim project ALU.circ as structural Verilog: 7 circuits, main circuit ALU
module ALU (
  input  [31:0] OperandA,
  input  [31:0] OperandB,
  input  [3:0] Operation,
  output [31:0] Result,
  output [31:0] High_Result,
  output Zero_Flag,
  output Negative_Flag
);

  wire comparator_2_lt, comparator_3_lt, undriven;
  wire [31:0] ADD, AND, DivHi, DivLo, DivuHi, DivuLo, MultHi, MultLo, MuluHi, MuluLo, NOR, OR, SLT, SLTU,
       SUB, XOR;

  Adder #(.width(32)) adder_1 (.a(OperandA), .b(OperandB), .out(ADD));  // open: cin, cout
  Subtractor #(.width(32)) subtractor_1 (.a(OperandA), .b(OperandB), .out(SUB));  // open: bin, bout
  Multiplier #(.width(32)) multiplier_1 (.a(OperandA), .b(OperandB), .out(MuluLo), .cout(MuluHi));  // open: cin
  Divider #(.width(32)) divider_1 (.a(OperandA), .b(OperandB), .out(DivuLo), .rem(DivuHi));  // open: upper
  Signed_Mult signed_mult_1 (.OperandA(OperandA), .Low(MultLo), .OperandB(OperandB), .High(MultHi));
  Signed_Div signed_div_1 (.OperandA(OperandA), .Low(DivLo), .OperandB(OperandB), .High(DivHi));
  Comparator #(.width(32)) comparator_1 (
    .a({32{1'b0}}), .b({Negative_Flag, Result[30:0]}), .eq(Zero_Flag));  // open: gt, lt
  Multiplexer #(.select(4), .width(32)) multiplexer_1 (
    .in0(ADD), .in1(SUB), .in2(AND), .in3(OR), .in4(NOR), .in5(XOR), .in6(SLT), .in7(SLTU), .in8(MuluLo),
    .in9(MultLo), .in10(DivuLo), .in11(DivLo), .out({Negative_Flag, Result[30:0]}), .sel(Operation),
    .en(undriven));  // open: in12, in13, in14, in15
  assign OR = OperandA | OperandB;  // OR_Gate or_1, 32 bits wide
  // Probe on OperandA
  // Probe on {Negative_Flag, Result[30:0]}
  // Probe on High_Result
  assign AND = OperandA & OperandB;  // AND_Gate and_1, 32 bits wide
  assign NOR = ~(OperandA | OperandB);  // NOR_Gate nor_1, 32 bits wide
  assign XOR = OperandA ^ OperandB;  // XOR_Gate xor_1, 32 bits wide
  // Probe on OperandB
  // Probe on Operation
  Multiplexer #(.select(2), .width(32), .enable("false")) multiplexer_2 (
    .in0(MuluHi), .in1(MultHi), .in2(DivHi), .in3(DivuHi), .out(High_Result), .sel(Operation[1:0]));
  Comparator #(.width(32)) comparator_2 (.a(OperandA), .b(OperandB), .lt(comparator_2_lt));  // open: gt, eq
  Comparator #(.width(32), .mode("unsigned")) comparator_3 (
    .a(OperandA), .b(OperandB), .lt(comparator_3_lt));  // open: gt, eq
  assign SLT = {{31{1'b0}}, comparator_2_lt};  // Bit_Extender bit_extender_1
  assign SLTU = {{31{1'b0}}, comparator_3_lt};  // Bit_Extender bit_extender_2

  assign Result[31] = Negative_Flag;

  // Other names for the same wires on the sheet: A[31:0] = OperandA; B[31:0] = OperandB; HiResult[31:0] = High_Result;
  //   OP[3:0] = Operation; OpHi[1:0] = Operation[1:0]; N = Negative_Flag; Z = Zero_Flag

  // Notes on the sheet:
  //   INPUTS
  //   ARITHMETIC INSTRUCTIONS
  //   OUTPUTS
  //   LOGIC INSTRUCTIONS
  //   VISUALIZE INPUTS/OUTPUTS 
  //   COMPARISON INSTRUCTIONS
endmodule

module Signed_Mult (
  input  [31:0] OperandA,
  input  [31:0] OperandB,
  output [31:0] Low,
  output [31:0] High
);

  wire negator_1_carryout, signA, signB, signResult;
  wire [31:0] absolute_value_1_abs_value, absolute_value_2_abs_value, adder_1_out, negator_1_neg_value,
       not_1_out, PosHi, PosLo;

  Absolute_Value absolute_value_1 (.OperandA(OperandA), .Abs_Value(absolute_value_1_abs_value), .Negative(signA));
  Absolute_Value absolute_value_2 (.OperandA(OperandB), .Abs_Value(absolute_value_2_abs_value), .Negative(signB));
  xor xor_1 (signResult, signA, signB);
  Multiplier #(.width(32)) multiplier_1 (
    .a(absolute_value_1_abs_value), .b(absolute_value_2_abs_value), .out(PosLo), .cout(PosHi));  // open: cin
  assign not_1_out = ~PosHi;  // NOT_Gate not_1, 32 bits wide
  Negator negator_1 (.OperandA(PosLo), .Neg_Value(negator_1_neg_value), .CarryOut(negator_1_carryout));
  Adder #(.width(32)) adder_1 (
    .a(not_1_out), .b({32{1'b0}}), .out(adder_1_out), .cin(negator_1_carryout));  // open: cout
  Multiplexer #(.width(32), .enable("false")) multiplexer_1 (
    .in0(PosLo), .in1(negator_1_neg_value), .out(Low), .sel(signResult));
  Multiplexer #(.width(32), .enable("false")) multiplexer_2 (
    .in0(adder_1_out), .in1(PosHi), .out(High), .sel(signResult));

  // Other names for the same wires on the sheet: A[31:0] = OperandA; B[31:0] = OperandB; Hi[31:0] = High;
  //   Lo[31:0] = Low

  // Notes on the sheet:
  //   INPUTS
  //   OUTPUTS
  //   NegHi
endmodule

module Absolute_Value (
  input  [31:0] OperandA,
  output [31:0] Abs_Value,
  output Negative
);

  wire [31:0] negator_1_neg_value;

  Negator negator_1 (.OperandA(OperandA), .Neg_Value(negator_1_neg_value));  // open: CarryOut
  Multiplexer #(.width(32), .enable("false")) multiplexer_1 (
    .in0(OperandA), .in1(negator_1_neg_value), .out(Abs_Value), .sel(OperandA[31]));

  assign Negative = OperandA[31];

  // Other names for the same wires on the sheet: A[31:0] = OperandA; Neg = OperandA[31]; AbsVal[31:0] = Abs_Value

  // Notes on the sheet:
  //   INPUTS
  //   OUTPUTS
endmodule

module Signed_Div (
  input  [31:0] OperandA,
  input  [31:0] OperandB,
  output [31:0] Low,
  output [31:0] High
);

  wire signA, signB, signResult;
  wire [31:0] absolute_value_1_abs_value, absolute_value_2_abs_value, negator_1_neg_value,
       negator_2_neg_value, PosHi, PosLo;

  Absolute_Value absolute_value_1 (.OperandA(OperandA), .Abs_Value(absolute_value_1_abs_value), .Negative(signA));
  Absolute_Value absolute_value_2 (.OperandA(OperandB), .Abs_Value(absolute_value_2_abs_value), .Negative(signB));
  xor xor_1 (signResult, signA, signB);
  Divider #(.width(32)) divider_1 (
    .a(absolute_value_1_abs_value), .b(absolute_value_2_abs_value), .out(PosLo), .rem(PosHi));  // open: upper
  Negator negator_1 (.OperandA(PosLo), .Neg_Value(negator_1_neg_value));  // open: CarryOut
  Negator negator_2 (.OperandA(PosHi), .Neg_Value(negator_2_neg_value));  // open: CarryOut
  Multiplexer #(.width(32), .enable("false")) multiplexer_1 (
    .in0(PosLo), .in1(negator_1_neg_value), .out(Low), .sel(signResult));
  Multiplexer #(.width(32), .enable("false")) multiplexer_2 (
    .in0(negator_2_neg_value), .in1(PosHi), .out(High), .sel(signResult));

  // Other names for the same wires on the sheet: A[31:0] = OperandA; B[31:0] = OperandB; Hi[31:0] = High;
  //   Lo[31:0] = Low

  // Notes on the sheet:
  //   INPUTS
  //   OUTPUTS
  //   NegHi
endmodule

module Negator (
  input  [31:0] OperandA,
  output [31:0] Neg_Value,
  output CarryOut
);

  wire [31:0] not_1_out;

  assign not_1_out = ~OperandA;  // NOT_Gate not_1, 32 bits wide
  Adder #(.width(32)) adder_1 (.a(not_1_out), .b(32'h1), .out(Neg_Value), .cout(CarryOut));  // open: cin

  // Other names for the same wires on the sheet: A[31:0] = OperandA; NegVal[31:0] = Neg_Value

  // Notes on the sheet:
  //   INPUTS
  //   OUTPUTS
endmodule

module ALU_INPUT (
  input  [31:0] RT,
  input  [15:0] Const,
  input  Const_Ext_Sel,
  input  Type_I,
  output [31:0] ALU_Input
);

  wire [31:0] const_extend_1_extended_const;

  CONST_EXTEND const_extend_1 (
    .Const(Const), .Extend_Selector(Const_Ext_Sel), .Extended_Const(const_extend_1_extended_const));
  Multiplexer #(.width(32), .disabled(0), .enable("false")) multiplexer_1 (
    .in0(RT), .in1(const_extend_1_extended_const), .out(ALU_Input), .sel(Type_I));

  // Other names for the same wires on the sheet: ALU_IN[31:0] = ALU_Input; EXTSEL = Const_Ext_Sel

  // Notes on the sheet:
  //   INPUT
  //   ALU INPUT SELECTION
  //   OUTPUT
endmodule

module CONST_EXTEND (
  input  [15:0] Const,
  input  Extend_Selector,
  output [31:0] Extended_Const
);

  wire [31:0] bit_extender_1_out, bit_extender_2_out;

  assign bit_extender_1_out = {{16{Const[15]}}, Const};  // Bit_Extender bit_extender_1
  assign bit_extender_2_out = {{16{1'b0}}, Const};  // Bit_Extender bit_extender_2
  Multiplexer #(.width(32), .disabled(0), .enable("false")) multiplexer_1 (
    .in0(bit_extender_1_out), .in1(bit_extender_2_out), .out(Extended_Const), .sel(Extend_Selector));

  // Other names for the same wires on the sheet: EXTENDED[31:0] = Extended_Const; SEL = Extend_Selector

  // Notes on the sheet:
  //   INPUT
  //   CONST EXTENSION
  //   OUTPUT
endmodule
