// Logisim project ALU_ENCODER.circ as structural Verilog: 1 circuit, main circuit ALU_ENCODER
module ALU_ENCODER (
  input  add,
  input  \and ,
  input  slt,
  input  addi,
  input  andi,
  input  slti,
  input  sub,
  input  \or ,
  input  sltu,
  input  ori,
  input  sltiu,
  input  mult,
  input  \xor ,
  input  multu,
  input  xori,
  input  div,
  input  \nor ,
  input  divu,
  output [3:0] ALU_OP
);

  wire ADD_t, AND_t, OR_t, priority_encoder_1_gs, SLT_t, SLTU_t, XOR_t;
  wire [3:0] priority_encoder_1_out;

  or or_1 (ADD_t, add, addi);
  Priority_Encoder #(.select(4), .disabled(0)) priority_encoder_1 (
    .in0(ADD_t), .in1(sub), .in2(SLT_t), .in3(SLTU_t), .in4(AND_t), .in5(OR_t), .in6(\nor ), .in7(XOR_t),
    .in8(mult), .in9(multu), .in10(div), .in11(divu), .out(priority_encoder_1_out),
    .gs(priority_encoder_1_gs), .en_in(1'b1));  // open: in12, in13, in14, in15, en_out
  or or_2 (AND_t, \and , andi);
  or or_3 (OR_t, \or , ori);
  or or_4 (XOR_t, \xor , xori);
  Multiplexer #(.width(4), .enable("false")) multiplexer_1 (
    .in0(4'b0000), .in1(priority_encoder_1_out), .out(ALU_OP), .sel(priority_encoder_1_gs));
  or or_5 (SLT_t, slt, slti);
  or or_6 (SLTU_t, sltu, sltiu);

  // Other names for the same wires on the sheet: MULU = multu

  // Notes on the sheet:
  //   ARITHMETIC
  //   ENCODING
  //   INPUT
  //   LOGIC
  //   CODES
  //   ADD - 0000
  //   SUB - 0001
  //   AND - 0010
  //   OR - 0011
  //   NOR - 0100
  //   XOR - 0101
  //   SLT - 0110
  //   SLTU - 0111
  //   MULTU - 1000
  //   MULT - 1001
  //   DIVU - 1010
  //   DIV - 1011
  //   COMPARISON
  //   OUTPUT
endmodule
