// Logisim project ALU_INPUT.circ as structural Verilog: 2 circuits, main circuit ALU_INPUT
module ALU_INPUT (
  input  [31:0] RT,
  input  [15:0] Const,
  input  Const_Ext_Sel,
  input  Type_I,
  output [31:0] ALU_Input
);

  wire [31:0] const_extend_1_extended_const;

  CONST_EXTEND const_extend_1 (
    .Const(Const), .Extend_Selector(Const_Ext_Sel), .Extended_Const(const_extend_1_extended_const));
  Multiplexer #(.width(32), .disabled(0), .enable("false")) multiplexer_1 (
    .in0(RT), .in1(const_extend_1_extended_const), .out(ALU_Input), .sel(Type_I));

  // Other names for the same wires on the sheet: ALU_IN[31:0] = ALU_Input; EXTSEL = Const_Ext_Sel

  // Notes on the sheet:
  //   INPUT
  //   ALU INPUT SELECTION
  //   OUTPUT
endmodule

module CONST_EXTEND (
  input  [15:0] Const,
  input  Extend_Selector,
  output [31:0] Extended_Const
);

  wire [31:0] bit_extender_1_out, bit_extender_2_out;

  assign bit_extender_1_out = {{16{Const[15]}}, Const};  // Bit_Extender bit_extender_1
  assign bit_extender_2_out = {{16{1'b0}}, Const};  // Bit_Extender bit_extender_2
  Multiplexer #(.width(32), .disabled(0), .enable("false")) multiplexer_1 (
    .in0(bit_extender_1_out), .in1(bit_extender_2_out), .out(Extended_Const), .sel(Extend_Selector));

  // Other names for the same wires on the sheet: EXTENDED[31:0] = Extended_Const; SEL = Extend_Selector

  // Notes on the sheet:
  //   INPUT
  //   CONST EXTENSION
  //   OUTPUT
endmodule
