// Logisim project BC_SELECTOR.circ as structural Verilog: 1 circuit, main circuit BC_SELECTOR
module BC_SELECTOR (
  input  beq,
  input  [1:0] BC_SELECTOR,
  input  bne,
  input  [2:0] FLAG_CONDITION,
  input  blez,
  input  bgtz,
  input  bltz,
  input  jr,
  input  j
);

  wire IS_BRANCH;
  wire [2:0] priority_encoder_1_out;

  Priority_Encoder priority_encoder_1 (
    .in0(beq), .in1(bne), .in2(blez), .in3(bgtz), .in4(bltz), .out(priority_encoder_1_out), .en_in(1'b1),
    .gs(IS_BRANCH));  // open: in5, in6, in7, en_out
  or or_1 (BC_SELECTOR[0], IS_BRANCH, jr);
  or or_2 (BC_SELECTOR[1], jr, j);
  Multiplexer #(.width(3), .disabled(0), .enable("false")) multiplexer_1 (
    .in0(3'b000), .in1(priority_encoder_1_out), .out(FLAG_CONDITION), .sel(IS_BRANCH));

  // Other names for the same wires on the sheet: CONDITION[2:0] = FLAG_CONDITION; SELECTOR[1:0] = BC_SELECTOR

  // Notes on the sheet:
  //   INPUTS
  //   Is Branch
  //   Or
  //   JR
  //   SELECTOR_CODES
  //   BIT 0
  //   BIT 1
  //   Jr
  //   Or
  //   J
  //   FLAG_CONDITION
  //   BC_SELECTOR
  //   OUTPUTS
  //   CONDITION_CODES
  //   BEQ - 000
  //   BNE - 001
  //   BLEZ - 010
  //   BGTZ - 011
  //   BLTZ - 100
endmodule
