// Logisim project BRANCH_CONTROL.circ as structural Verilog: 1 circuit, main circuit BRANCH_CONTROL
module BRANCH_CONTROL (
  input  [31:0] RS,
  input  [25:0] JS,
  input  [31:0] RT,
  input  [15:0] Offset,
  input  [1:0] Branch_Selector,
  input  [31:0] IA,
  input  [2:0] Flag_Condition,
  output [31:0] NIA
);

  wire comparator_2_eq, CONDITION, RS__0, RS__0_t, RS___0, RS____RT, RS____RT_t;
  wire [31:0] bit_extender_1_out, IA_4, IA_4_X, multiplexer_1_out, NOFF;

  Comparator #(.width(32)) comparator_1 (.a(RS), .b(RT), .eq(RS____RT_t));  // open: gt, lt
  not not_1 (RS____RT, RS____RT_t);
  Comparator #(.width(32)) comparator_2 (.a(RS), .b({32{1'b0}}), .gt(RS__0_t), .eq(comparator_2_eq), .lt(RS__0));
  Adder #(.width(32)) adder_1 (.a(IA), .b(32'h4), .out(IA_4));  // open: cin, cout
  Adder #(.width(32)) adder_2 (.a(IA_4), .b(NOFF), .out(IA_4_X));  // open: cin, cout
  Multiplexer #(.width(32), .disabled(0), .enable("false")) multiplexer_1 (
    .in0(IA_4), .in1(IA_4_X), .out(multiplexer_1_out), .sel(CONDITION));
  or or_1 (RS___0, comparator_2_eq, RS__0);
  Multiplexer #(.select(2), .width(32), .disabled(0), .enable("false")) multiplexer_2 (
    .in0(IA_4), .in1(multiplexer_1_out), .in2({IA[31:28], JS, 2'b00}), .in3(RS), .out(NIA),
    .sel(Branch_Selector));
  assign bit_extender_1_out = {{16{Offset[15]}}, Offset};  // Bit_Extender bit_extender_1
  Multiplexer #(.select(3), .disabled(0), .enable("false")) multiplexer_3 (
    .in0(RS____RT_t), .in1(RS____RT), .in2(RS__0_t), .in3(RS___0), .in4(RS__0), .out(CONDITION),
    .sel(Flag_Condition));  // open: in5, in6, in7
  Shifter #(.width(32)) shifter_1 (.in(bit_extender_1_out), .\dist (5'b00010), .out(NOFF));

  // Other names for the same wires on the sheet: BS[1:0] = Branch_Selector; FC[2:0] = Flag_Condition;
  //   JUMP[31:2] = {IA[31:28], JS}; OFF[15:0] = Offset

  // Notes on the sheet:
  //   INSTRUCTION ADRESS + 4
  //   TARGET = IA + 4 + EXTENDED OFFSET
  //   INPUT
  //   BRANCH CONDITIONS CHECK
  //   NEW INSTRUCTION ADRESS SELECTION
  //   OUTPUT
  //   JUMP CALC
  //   EXTENDED OFFSET
  //   CONDITION SELECTION
endmodule
