// Logisim project CacheController.circ as structural Verilog: 1 circuit, main circuit Cache Controller
module Cache_Controller (
  input  ready_to_read,
  input  ready_to_write,
  input  [31:0] Address,
  input  [31:0] RAM_Data0,
  input  [31:0] DataInput,
  input  [31:0] RAM_Data1,
  input  [31:0] Ram_Single_Data_Out,
  input  Read,
  input  write,
  input  [31:0] RAM_Data2,
  input  cacheEnable,
  input  Clk,
  input  [31:0] RAM_Data3,
  input  Rst,
  output ready,
  output [31:0] toRamData0,
  output [31:0] dataOut,
  output [31:0] ToRAM_Data1,
  output [31:0] toRamAddr,
  output [31:0] ToRAM_Data2,
  output ToRamRead,
  output ToRamWrite,
  output [31:0] ToRAM_Data3,
  output [31:0] To_Ram_DataIn_Single
);

  wire and_1_out, and_2_out, and_3_out, and_4_out, and_5_out, and_6_out, and_8_out, and_9_out, and_10_out,
       and_11_out, and_12_out, and_13_out, and_15_out, and_17_out, and_18_out, and_19_out, and_20_out,
       and_21_out, and_22_out, and_24_out, and_25_out, and_26_out, and_27_out, and_28_out, and_29_out,
       and_30_out, and_31_out, and_32_out, and_33_out, and_34_out, and_35_out, and_37_out, bit1, bit2,
       Cache_Dirty_Out, Cache_Valid_Out, Col_En_0, Col_En_1, Col_En_2, Col_En_3, Dirty_Reg_0, Dirty_Reg_1,
       Dirty_Reg_2, Dirty_Reg_3, FSM_Clear_Dirty, FSM_Fetch_En, FSM_Set_Valid_En, FSM_System_Ready,
       FSM_Write_Enable, FSM_Write_Hit_En, Hit, Is_IDLE, Is_WRITE_BACK, Line_En_0, Line_En_1, Line_En_2,
       Line_En_3, Miss, or_1_out, or_2_out, or_3_out, or_4_out, or_8_out, or_9_out, tag_match, Valid_Reg_0,
       Valid_Reg_1, Valid_Reg_2, Valid_Reg_3, Write_Block_Active;
  wire [1:0] Current_State;
  wire [9:0] Cache_Tag_Out, multiplexer_1_out, multiplexer_2_out, multiplexer_3_out, multiplexer_7_out,
       Tag_Reg_0, Tag_Reg_1, Tag_Reg_2, Tag_Reg_3;
  wire [31:0] Data_In_Col0, Data_In_Col1, Data_In_Col2, Data_In_Col3, FSM_RAM_Addr, L0W0, L0W1, L0W2, L0W3,
       L1W0, L1W1, L1W2, L1W3, L2W0, L2W1, L2W2, L2W3, L3W0, L3W1, L3W2, L3W3, undriven, W0_Selected,
       W1_Selected, W2_Selected, W3_Selected, Word_To_CPU;
  wire [31:16] CPU_Block_Addr, WB_Block_Addr;

  and and_1 (and_1_out, Line_En_0, FSM_Write_Hit_En);
  and and_2 (and_2_out, Line_En_0, Col_En_0, FSM_Write_Enable);
  and and_3 (and_3_out, Line_En_1, Col_En_0, FSM_Write_Enable);
  and and_4 (and_4_out, Line_En_2, Col_En_0, FSM_Write_Enable);
  and and_5 (and_5_out, Line_En_3, Col_En_0, FSM_Write_Enable);
  Register #(.width(1)) register_1 (.D(1'b1), .en(and_6_out), .Q(Valid_Reg_0), .clk(Clk), .clr(Rst));
  and and_6 (and_6_out, Line_En_0, FSM_Set_Valid_En);
  Register #(.width(1)) register_2 (.D(1'b1), .en(and_1_out), .Q(Dirty_Reg_0), .clk(Clk), .clr(or_1_out));
  or or_1 (or_1_out, Rst, FSM_Clear_Dirty);
  Register #(.width(32)) register_3 (.D(Data_In_Col0), .en(and_2_out), .Q(L0W0), .clk(Clk), .clr(Rst));
  Register #(.width(32)) register_4 (.D(Data_In_Col0), .en(and_3_out), .Q(L1W0), .clk(Clk), .clr(Rst));
  Register #(.width(32)) register_5 (.D(Data_In_Col0), .en(and_4_out), .Q(L2W0), .clk(Clk), .clr(Rst));
  Register #(.width(32)) register_6 (.D(Data_In_Col0), .en(and_5_out), .Q(L3W0), .clk(Clk), .clr(Rst));
  and and_7 (FSM_Set_Valid_En, FSM_Fetch_En, ready_to_read);
  Register #(.width(2)) register_7 (.D({bit2, bit1}), .en(cacheEnable), .Q(Current_State), .clk(Clk), .clr(Rst));
  Multiplexer #(.width(10), .enable("false")) multiplexer_1 (
    .in0({10{1'b0}}), .in1(Address[15:6]), .out(multiplexer_1_out), .sel(FSM_Fetch_En));
  Comparator #(.width(10)) comparator_1 (.a(Cache_Tag_Out), .b(Address[15:6]), .eq(tag_match));  // open: gt, lt
  Register #(.width(10)) register_8 (.D(multiplexer_1_out), .en(and_8_out), .Q(Tag_Reg_0), .clk(Clk), .clr(Rst));
  and and_8 (and_8_out, Line_En_0, FSM_Fetch_En);
  and and_9 (and_9_out, Line_En_0, FSM_Write_Hit_En);
  Register #(.width(32)) register_9 (.D(Data_In_Col1), .en(and_10_out), .Q(L0W1), .clk(Clk), .clr(Rst));
  and and_10 (and_10_out, Line_En_0, Col_En_1, FSM_Write_Enable);
  Register #(.width(32)) register_10 (.D(Data_In_Col1), .en(and_11_out), .Q(L1W1), .clk(Clk), .clr(Rst));
  and and_11 (and_11_out, Line_En_1, Col_En_1, FSM_Write_Enable);
  Register #(.width(32)) register_11 (.D(Data_In_Col1), .en(and_12_out), .Q(L2W1), .clk(Clk), .clr(Rst));
  and and_12 (and_12_out, Line_En_2, Col_En_1, FSM_Write_Enable);
  Register #(.width(32)) register_12 (.D(Data_In_Col1), .en(and_13_out), .Q(L3W1), .clk(Clk), .clr(Rst));
  and and_13 (and_13_out, Line_En_3, Col_En_1, FSM_Write_Enable);
  Decoder #(.select(2), .enable("false")) decoder_1 (
    .out0(Is_IDLE), .out1(Is_WRITE_BACK), .out2(FSM_Fetch_En), .sel(Current_State));  // open: out3
  or or_2 (or_2_out, Read, write);
  and and_14 (Hit, or_2_out, Cache_Valid_Out, tag_match);
  not not_1 (Miss, Hit);
  and and_15 (and_15_out, Line_En_1, FSM_Set_Valid_En);
  Register #(.width(1)) register_13 (.D(1'b1), .en(and_9_out), .Q(Dirty_Reg_1), .clk(Clk), .clr(or_3_out));
  or or_3 (or_3_out, Rst, FSM_Clear_Dirty);
  and and_16 (FSM_Clear_Dirty, Is_WRITE_BACK, ready_to_write);
  Register #(.width(1)) register_14 (.D(1'b1), .en(and_15_out), .Q(Valid_Reg_1), .clk(Clk), .clr(Rst));
  Multiplexer #(.width(10), .enable("false")) multiplexer_2 (
    .in0({10{1'b0}}), .in1(Address[15:6]), .out(multiplexer_2_out), .sel(FSM_Fetch_En));
  and and_17 (and_17_out, Line_En_1, FSM_Fetch_En);
  and and_18 (and_18_out, Line_En_0, Col_En_2, FSM_Write_Enable);
  and and_19 (and_19_out, Line_En_1, Col_En_2, FSM_Write_Enable);
  and and_20 (and_20_out, Line_En_2, Col_En_2, FSM_Write_Enable);
  and and_21 (and_21_out, Line_En_3, Col_En_2, FSM_Write_Enable);
  and and_22 (and_22_out, Is_IDLE, Hit);
  and and_23 (FSM_Write_Hit_En, Is_IDLE, Hit, write);
  Register #(.width(10)) register_15 (.D(multiplexer_2_out), .en(and_17_out), .Q(Tag_Reg_1), .clk(Clk), .clr(Rst));
  Register #(.width(1)) register_16 (.D(1'b1), .en(and_24_out), .Q(Dirty_Reg_2), .clk(Clk), .clr(or_4_out));
  and and_24 (and_24_out, Line_En_0, FSM_Write_Hit_En);
  or or_4 (or_4_out, Rst, FSM_Clear_Dirty);
  Register #(.width(32)) register_17 (.D(Data_In_Col2), .en(and_18_out), .Q(L0W2), .clk(Clk), .clr(Rst));
  Register #(.width(32)) register_18 (.D(Data_In_Col2), .en(and_19_out), .Q(L1W2), .clk(Clk), .clr(Rst));
  Register #(.width(32)) register_19 (.D(Data_In_Col2), .en(and_20_out), .Q(L2W2), .clk(Clk), .clr(Rst));
  Register #(.width(32)) register_20 (.D(Data_In_Col2), .en(and_21_out), .Q(L3W2), .clk(Clk), .clr(Rst));
  or or_5 (bit1, and_27_out, and_28_out);
  or or_6 (FSM_System_Ready, and_22_out, and_25_out);
  and and_25 (and_25_out, FSM_Fetch_En, ready_to_read);
  and and_26 (and_26_out, Line_En_2, FSM_Set_Valid_En);
  and and_27 (and_27_out, Is_IDLE, Miss, ~Cache_Dirty_Out);  // AND_Gate
  and and_28 (and_28_out, Is_WRITE_BACK, ready_to_write);
  Multiplexer #(.width(10), .enable("false")) multiplexer_3 (
    .in0({10{1'b0}}), .in1(Address[15:6]), .out(multiplexer_3_out), .sel(FSM_Fetch_En));
  Register #(.width(1)) register_21 (.D(1'b1), .en(and_26_out), .Q(Valid_Reg_2), .clk(Clk), .clr(Rst));
  Register #(.width(10)) register_22 (.D(multiplexer_3_out), .en(and_29_out), .Q(Tag_Reg_2), .clk(Clk), .clr(Rst));
  and and_29 (and_29_out, Line_En_0, FSM_Fetch_En);
  and and_30 (and_30_out, Line_En_0, FSM_Write_Hit_En);
  and and_31 (and_31_out, Line_En_0, Col_En_3, FSM_Write_Enable);
  and and_32 (and_32_out, Line_En_1, Col_En_3, FSM_Write_Enable);
  and and_33 (and_33_out, Line_En_2, Col_En_3, FSM_Write_Enable);
  and and_34 (and_34_out, Line_En_3, Col_En_3, FSM_Write_Enable);
  or or_7 (FSM_Write_Enable, FSM_Fetch_En, FSM_Write_Hit_En);
  Register #(.width(1)) register_23 (.D(1'b1), .en(and_30_out), .Q(Dirty_Reg_3), .clk(Clk), .clr(or_8_out));
  or or_8 (or_8_out, Rst, FSM_Clear_Dirty);
  Register #(.width(32)) register_24 (.D(Data_In_Col3), .en(and_31_out), .Q(L0W3), .clk(Clk), .clr(Rst));
  Register #(.width(32)) register_25 (.D(Data_In_Col3), .en(and_32_out), .Q(L1W3), .clk(Clk), .clr(Rst));
  Register #(.width(32)) register_26 (.D(Data_In_Col3), .en(and_33_out), .Q(L2W3), .clk(Clk), .clr(Rst));
  Register #(.width(32)) register_27 (.D(Data_In_Col3), .en(and_34_out), .Q(L3W3), .clk(Clk), .clr(Rst));
  Register #(.width(1)) register_28 (.D(1'b1), .en(and_35_out), .Q(Valid_Reg_3), .clk(Clk), .clr(Rst));
  and and_35 (and_35_out, Line_En_3, FSM_Set_Valid_En);
  and and_36 (bit2, Is_IDLE, Miss, Cache_Dirty_Out);
  Multiplexer #(.width(32), .enable("false")) multiplexer_4 (
    .in0(Ram_Single_Data_Out), .in1(Word_To_CPU), .out(dataOut), .sel(cacheEnable));
  or or_9 (or_9_out, ready_to_read, ready_to_write);
  Multiplexer #(.enable("false")) multiplexer_5 (.in0(Read), .in1(FSM_Fetch_En), .out(ToRamRead), .sel(cacheEnable));
  Multiplexer #(.enable("false")) multiplexer_6 (.in0(write), .in1(FSM_Fetch_En), .out(ToRamWrite), .sel(cacheEnable));
  Multiplexer #(.width(10), .enable("false")) multiplexer_7 (
    .in0({10{1'b0}}), .in1(Address[15:6]), .out(multiplexer_7_out), .sel(FSM_Fetch_En));
  Multiplexer #(.enable("false")) multiplexer_8 (
    .in0(or_9_out), .in1(FSM_System_Ready), .out(ready), .sel(cacheEnable));
  Register #(.width(10)) register_29 (.D(multiplexer_7_out), .en(and_37_out), .Q(Tag_Reg_3), .clk(Clk), .clr(Rst));
  and and_37 (and_37_out, Line_En_0, FSM_Fetch_En);
  Multiplexer #(.select(2), .enable("false")) multiplexer_9 (
    .in0(Dirty_Reg_0), .in1(Dirty_Reg_1), .in2(Dirty_Reg_2), .in3(Dirty_Reg_3), .out(Cache_Dirty_Out),
    .sel(Address[5:4]));
  Multiplexer #(.select(2), .width(32), .enable("false")) multiplexer_10 (
    .in0(L0W0), .in1(L1W0), .in2(L2W0), .in3(L3W0), .out(W0_Selected), .sel(Address[5:4]));
  Multiplexer #(.select(2), .width(32), .enable("false")) multiplexer_11 (
    .in0(L0W1), .in1(L1W1), .in2(L2W1), .in3(L3W1), .out(W1_Selected), .sel(Address[5:4]));
  Multiplexer #(.select(2), .width(32), .enable("false")) multiplexer_12 (
    .in0(L0W2), .in1(L1W2), .in2(L2W2), .in3(L3W2), .out(W2_Selected), .sel(Address[5:4]));
  Multiplexer #(.select(2), .width(32), .enable("false")) multiplexer_13 (
    .in0(L0W3), .in1(L1W3), .in2(L2W3), .in3(L3W3), .out(W3_Selected), .sel(Address[5:4]));
  Multiplexer #(.width(32), .enable("false")) multiplexer_14 (
    .in0(Address), .in1(FSM_RAM_Addr), .out(toRamAddr), .sel(cacheEnable));
  Multiplexer #(.width(32), .enable("false")) multiplexer_15 (
    .in0(DataInput), .in1({32{1'b0}}), .out(To_Ram_DataIn_Single), .sel(cacheEnable));
  Multiplexer #(.select(2), .enable("false")) multiplexer_16 (
    .in0(Valid_Reg_0), .in1(Valid_Reg_1), .in2(Valid_Reg_2), .in3(Valid_Reg_3), .out(Cache_Valid_Out),
    .sel(Address[5:4]));
  Multiplexer #(.enable("false")) multiplexer_17 (
    .in0(1'b0), .in1(Is_WRITE_BACK), .out(Write_Block_Active), .sel(cacheEnable));
  Multiplexer #(.width(32), .enable("false")) multiplexer_18 (
    .in0(DataInput), .in1(RAM_Data0), .out(Data_In_Col0), .sel(FSM_Fetch_En));
  Multiplexer #(.width(32), .enable("false")) multiplexer_19 (
    .in0(DataInput), .in1(RAM_Data1), .out(Data_In_Col1), .sel(FSM_Fetch_En));
  Multiplexer #(.width(32), .enable("false")) multiplexer_20 (
    .in0(DataInput), .in1(RAM_Data2), .out(Data_In_Col2), .sel(FSM_Fetch_En));
  Multiplexer #(.width(32), .enable("false")) multiplexer_21 (
    .in0(DataInput), .in1(RAM_Data3), .out(Data_In_Col3), .sel(FSM_Fetch_En));
  Multiplexer #(.width(32), .enable("false")) multiplexer_22 (
    .in0({CPU_Block_Addr, Address[15:4], 4'b0000}),
    .in1({WB_Block_Addr, Cache_Tag_Out, Address[5:4], 4'b0000}), .out(FSM_RAM_Addr), .sel(Is_WRITE_BACK));
  Multiplexer #(.select(2), .width(10), .enable("false")) multiplexer_23 (
    .in0(Tag_Reg_0), .in1(Tag_Reg_1), .in2(Tag_Reg_2), .in3(Tag_Reg_3), .out(Cache_Tag_Out),
    .sel(Address[5:4]));
  Multiplexer #(.width(32), .enable("false")) multiplexer_24 (
    .in0({32{1'b0}}), .in1(W2_Selected), .out(ToRAM_Data2), .sel(Write_Block_Active));
  Multiplexer #(.width(32), .enable("false")) multiplexer_25 (
    .in0({32{1'b0}}), .in1(W0_Selected), .out(toRamData0), .sel(Write_Block_Active));
  Decoder #(.select(2), .enable("false")) decoder_2 (
    .out0(Line_En_0), .out1(Line_En_1), .out2(Line_En_2), .out3(Line_En_3), .sel(Address[5:4]));
  Decoder #(.select(2), .enable("false")) decoder_3 (
    .out0(Col_En_0), .out1(Col_En_1), .out2(Col_En_2), .out3(Col_En_3), .sel(Address[3:2]));
  Multiplexer #(.select(2), .width(32), .enable("false")) multiplexer_26 (
    .in0(W0_Selected), .in1(W1_Selected), .in2(undriven), .in3(W3_Selected), .out(Word_To_CPU),
    .sel(Address[3:2]));
  Multiplexer #(.width(32), .enable("false")) multiplexer_27 (
    .in0({32{1'b0}}), .in1(W3_Selected), .out(ToRAM_Data3), .sel(Write_Block_Active));
  Multiplexer #(.width(32), .enable("false")) multiplexer_28 (
    .in0({32{1'b0}}), .in1(W1_Selected), .out(ToRAM_Data1), .sel(Write_Block_Active));

  // Other names for the same wires on the sheet: addr[31:0] = Address; word_select[1:0] = Address[3:2];
  //   cacheEn = cacheEnable; CPU_Block_Addr[15:4] = Address[15:4]; tag[9:0] = Address[15:6]; dataIn[31:0] = DataInput;
  //   Is_FETCH = FSM_Fetch_En; toRamData1[31:0] = ToRAM_Data1; toRamData2[31:0] = ToRAM_Data2;
  //   toRamData3[31:0] = ToRAM_Data3; index[1:0] = Address[5:4]; WB_Block_Addr[15:4] = {Cache_Tag_Out, Address[5:4]}

  // Notes on the sheet:
  //   INPUTS
  //   DATA PATH
  //   Tag Registers
  //   Valid  Registers
  //   Dirty  Registers
  //   16  Registers Array
  //   CONTROL UNIT
  //   OUTPUTS
endmodule
