// Logisim project Control Unit.circ as structural Verilog: 1 circuit, main circuit Control Unit
module Control_Unit (
  input  CLK,
  input  ready_to_read,
  input  RST,
  input  ready_to_write,
  input  isRF,
  input  halt,
  input  isJmp,
  input  is_kbd,
  input  isRead,
  input  is_tty,
  input  HI_LO,
  input  isWrite,
  output fetch_data,
  output kbd_enable,
  output write_data,
  output \end ,
  output PC_enable,
  output HI_LO_enable,
  output RF_enable,
  output is_instruction,
  output Instruction_Memory_enable,
  output tty_enable
);

  wire demultiplexer_2_out0, demultiplexer_2_out1, demultiplexer_3_out0, demultiplexer_3_out1,
       demultiplexer_5_out0, demultiplexer_6_out3, END_q, end_read, end_write, fetch_data0, fetch_data1,
       Fetch_Instr_q, Idle_q, isPC, memAccess, memory, multiplexer_1_out, not_1_out, or_2_out, or_4_out, PC,
       RF, Save_Instr_q, Save_q, Wait_for_RAM_q;
  wire [1:0] execution_select;

  or or_1 (memAccess, isWrite, isRead);
  or or_2 (or_2_out, demultiplexer_2_out0, RST);
  nor nor_1 (isPC, memAccess, isRF);
  Demultiplexer #(.enable("false")) demultiplexer_1 (.out0(fetch_data1), .out1(write_data), .in(memory), .sel(isWrite));
  or or_3 (RF_enable, end_read, RF);
  Priority_Encoder #(.select(2)) priority_encoder_1 (
    .in0(isRF), .in1(memAccess), .in2(isPC), .in3(halt), .out(execution_select), .en_in(1'b1));  // open: gs, en_out
  D_Flip_Flop Idle (.clk(CLK), .D(or_2_out), .Q(Idle_q));  // open: Qn, preset, en, reset
  Demultiplexer #(.enable("false")) demultiplexer_2 (
    .out0(demultiplexer_2_out0), .out1(demultiplexer_2_out1), .in(Idle_q), .sel(not_1_out));
  not not_1 (not_1_out, RST);
  or or_4 (or_4_out, demultiplexer_3_out0, memory);
  or or_5 (fetch_data0, PC_enable, demultiplexer_2_out1);
  D_Flip_Flop Wait_for_RAM (.clk(CLK), .D(or_4_out), .Q(Wait_for_RAM_q), .reset(RST));  // open: Qn, preset, en
  D_Flip_Flop Save (.clk(CLK), .D(RF_enable), .Q(Save_q), .reset(RST));  // open: Qn, preset, en
  Demultiplexer #(.enable("false")) demultiplexer_3 (
    .out0(demultiplexer_3_out0), .out1(demultiplexer_3_out1), .in(Wait_for_RAM_q), .sel(multiplexer_1_out));
  Multiplexer #(.enable("false")) multiplexer_1 (
    .in0(ready_to_read), .in1(ready_to_write), .out(multiplexer_1_out), .sel(isWrite));
  or or_6 (is_instruction, demultiplexer_5_out0, fetch_data0);
  Demultiplexer #(.enable("false")) demultiplexer_4 (
    .out0(end_read), .out1(end_write), .in(demultiplexer_3_out1), .sel(isWrite));
  or or_7 (PC_enable, Save_q, end_write, PC);
  or or_8 (fetch_data, fetch_data0, fetch_data1);
  and and_1 (kbd_enable, PC_enable, is_kbd);
  D_Flip_Flop Fetch_Instr (.clk(CLK), .D(is_instruction), .Q(Fetch_Instr_q), .reset(RST));  // open: Qn, preset, en
  Demultiplexer #(.enable("false")) demultiplexer_5 (
    .out0(demultiplexer_5_out0), .out1(Instruction_Memory_enable), .in(Fetch_Instr_q), .sel(ready_to_read));
  D_Flip_Flop Save_Instr (
    .clk(CLK), .D(Instruction_Memory_enable), .Q(Save_Instr_q), .reset(RST));  // open: Qn, preset, en
  Demultiplexer #(.select(2), .enable("false")) demultiplexer_6 (
    .out0(RF), .out1(memory), .out2(PC), .out3(demultiplexer_6_out3), .in(Save_Instr_q),
    .sel(execution_select));
  and and_2 (HI_LO_enable, PC_enable, HI_LO);
  and and_3 (tty_enable, PC_enable, is_tty);
  or or_9 (\end , END_q, demultiplexer_6_out3);
  D_Flip_Flop u_END (.clk(CLK), .D(\end ), .Q(END_q), .reset(RST));  // open: Qn, preset, en

  // Other names for the same wires on the sheet: Inst_Mem_enable = Instruction_Memory_enable; HI_LO_t = PC_enable;
  //   kbd_clear = PC_enable; next_instruction = PC_enable; tty_out = PC_enable; use_HI_LO = HI_LO

  // Notes on the sheet:
  //   INPUTS
  //   ACCESS TO MEMORY?
  //   EXECUTION ORDER
  //   GLOBAL FETCH DATA
  //   ACTIVATE KBD?
  //   OUTPUTS
  //   USE HI-LO?
  //   WRITE TO TERMINAL?
endmodule
