// Logisim project HI-LO Registers.circ as structural Verilog: 1 circuit, main circuit HI/LO Registers
module HI_LO_Registers (
  input  [31:0] HI_in,
  input  [31:0] Lo_in,
  input  HI_LO_enable,
  input  Reset,
  input  Clock,
  output [31:0] OutputHi,
  output [31:0] OutputLo
);

  Register #(.width(32), .trigger("falling")) RegisterHi (
    .D(HI_in), .en(HI_LO_enable), .Q(OutputHi), .clk(Clock), .clr(Reset));
  Register #(.width(32), .trigger("falling")) RegisterLo (
    .D(Lo_in), .en(HI_LO_enable), .Q(OutputLo), .clk(Clock), .clr(Reset));

  // Other names for the same wires on the sheet: CLK = Clock; Hi[31:0] = HI_in; HI_LO_EN = HI_LO_enable;
  //   Lo[31:0] = Lo_in; OutHi[31:0] = OutputHi; OutLo[31:0] = OutputLo; Rst = Reset

  // Notes on the sheet:
  //   INPUTS
  //   OUTPUTS
endmodule
