// Logisim project INSTRUCTION_MEMORY.circ as structural Verilog: 1 circuit, main circuit INSTRUCTION_MEMORY
module INSTRUCTION_MEMORY (
  input  [31:0] Instruction,
  input  EN,
  input  Clk,
  input  Rst,
  output [31:0] Output
);

  Register #(.width(32)) register_1 (.D(Instruction), .en(EN), .Q(Output), .clk(Clk), .clr(Rst));

  // Notes on the sheet:
  //   INSTRUCTION MEMORY
endmodule
