// Logisim project IS_RF.circ as structural Verilog: 1 circuit, main circuit IS_RF
module IS_RF (
  input  nwrj,
  input  HI_LO,
  input  kbd,
  input  halt,
  input  rnd,
  input  tty,
  input  mfhi,
  input  nop,
  input  mflo,
  output Is_RF
);

  wire nor_1_out, or_1_out;

  or or_1 (or_1_out, nwrj, kbd, rnd, mfhi, mflo);
  nor nor_1 (nor_1_out, HI_LO, halt, tty, nop);
  and and_1 (Is_RF, or_1_out, nor_1_out);

  // Notes on the sheet:
  //   NWRJ = Not Write, Read or Jump
  //   INPUTS
  //   VERIFICATION
  //   OUPUT
endmodule
