// Logisim project InstructionDecoder.circ as structural Verilog: 1 circuit, main circuit Instruction Decoder
module Instruction_Decoder (
  input  [31:0] Instruction,
  input  Write_Instr,
  input  Clck,
  input  Rst,
  input  isInstr,
  output [4:0] Rs,
  output read,
  output [2:0] InputToRF,
  output push,
  output kbd,
  output offsetSelect,
  output [4:0] Rt,
  output write,
  output [1:0] BC_Select,
  output pop,
  output HI_LO,
  output halt,
  output sw,
  output [2:0] BC_Flag,
  output [25:0] Jump_Address,
  output [3:0] ALU_Op,
  output tty,
  output [4:0] dataAddress,
  output jump,
  output rnd,
  output [15:0] offset,
  output [1:0] MemAddrSelect,
  output IsRF,
  output Type_I
);

  wire _00_0000, _11_1000, _11_1111, add, addi, \and , and_15_out, andi, beq, bgtz, blez, bltz, bne,
       comparator_2_eq, comparator_3_eq, comparator_4_eq, comparator_5_eq, comparator_6_eq, comparator_7_eq,
       comparator_10_eq, comparator_11_eq, comparator_12_eq, comparator_13_eq, comparator_18_eq,
       comparator_19_eq, comparator_22_eq, comparator_23_eq, comparator_30_eq, comparator_31_eq,
       comparator_34_eq, comparator_35_eq, comparator_36_eq, comparator_37_eq, comparator_38_eq,
       comparator_39_eq, div, divu, j, jr, lw, mfhi, mflo, mult, mulu, nop, \nor , nwrj, \or , or_6_out, ori,
       slt, slti, sltiu, sltu, sub, \xor , xori;
  wire [31:26] Instruction_t;

  Comparator #(.width(6)) comparator_1 (.a(Instruction_t), .b({6{1'b0}}), .eq(_00_0000));  // open: gt, lt
  Register #(.width(32), .trigger("falling")) Instruction_Memory (
    .D(Instruction), .en(Write_Instr), .Q({Instruction_t, Jump_Address}), .clk(Clck), .clr(Rst));
  Comparator #(.width(6)) comparator_2 (.a(Jump_Address[5:0]), .b(6'b100000), .eq(comparator_2_eq));  // open: gt, lt
  Comparator #(.width(6)) comparator_3 (.a(Jump_Address[5:0]), .b(6'b100010), .eq(comparator_3_eq));  // open: gt, lt
  Comparator #(.width(6)) comparator_4 (.a(Jump_Address[5:0]), .b(6'b011000), .eq(comparator_4_eq));  // open: gt, lt
  Comparator #(.width(6)) comparator_5 (.a(Jump_Address[5:0]), .b(6'b011010), .eq(comparator_5_eq));  // open: gt, lt
  Comparator #(.width(6)) comparator_6 (.a(Jump_Address[5:0]), .b(6'b011001), .eq(comparator_6_eq));  // open: gt, lt
  Comparator #(.width(6)) comparator_7 (.a(Jump_Address[5:0]), .b(6'b011011), .eq(comparator_7_eq));  // open: gt, lt
  Comparator #(.width(6)) comparator_8 (.a(Instruction_t), .b(6'b001000), .eq(addi));  // open: gt, lt
  or or_1 (read, pop, push);
  or or_2 (write, push, sw);
  or or_3 (jump, BC_Select[0], BC_Select[1]);
  and and_1 (add, _00_0000, comparator_2_eq);
  and and_2 (sub, _00_0000, comparator_3_eq);
  and and_3 (mult, _00_0000, comparator_4_eq);
  and and_4 (div, _00_0000, comparator_5_eq);
  and and_5 (mulu, _00_0000, comparator_6_eq);
  and and_6 (divu, _00_0000, comparator_7_eq);
  ALU_ENCODER alu_encoder_1 (
    .add(add), .\and (\and ), .slt(slt), .addi(addi), .andi(andi), .slti(slt), .sub(add), .\or (\or ),
    .sltu(sltu), .ori(ori), .sltiu(sltiu), .mult(mult), .\xor (\xor ), .multu(mulu), .xori(xori), .div(div),
    .\nor (\nor ), .divu(divu), .ALU_OP(ALU_Op));
  MA_INPUT_SELECTOR ma_input_selector_1 (
    .pop(pop), .push(push), .sw(sw), .lw(lw), .BC_SELECTOR(MemAddrSelect), .isInst(isInstr));
  Comparator #(.width(6)) comparator_9 (.a(Instruction_t), .b(6'b111000), .eq(_11_1000));  // open: gt, lt
  and and_7 (\and , _00_0000, comparator_10_eq);
  Comparator #(.width(6)) comparator_10 (.a(Jump_Address[5:0]), .b(6'b100100), .eq(comparator_10_eq));  // open: gt, lt
  and and_8 (\or , _00_0000, comparator_11_eq);
  Comparator #(.width(6)) comparator_11 (.a(Jump_Address[5:0]), .b(6'b100101), .eq(comparator_11_eq));  // open: gt, lt
  Comparator #(.width(6)) comparator_12 (.a(Jump_Address[5:0]), .b(6'b100111), .eq(comparator_12_eq));  // open: gt, lt
  Comparator #(.width(6)) comparator_13 (.a(Jump_Address[5:0]), .b(6'b101000), .eq(comparator_13_eq));  // open: gt, lt
  Comparator #(.width(6)) comparator_14 (.a(Instruction_t), .b(6'b001100), .eq(andi));  // open: gt, lt
  Comparator #(.width(6)) comparator_15 (.a(Instruction_t), .b(6'b001101), .eq(ori));  // open: gt, lt
  Comparator #(.width(6)) comparator_16 (.a(Instruction_t), .b(6'b001110), .eq(xori));  // open: gt, lt
  or or_4 (HI_LO, mulu, mulu, divu, div);
  and and_9 (\nor , _00_0000, comparator_12_eq);
  and and_10 (\xor , _00_0000, comparator_13_eq);
  IS_RF is_rf_1 (
    .nwrj(nwrj), .HI_LO(HI_LO), .kbd(kbd), .halt(halt), .rnd(rnd), .tty(nop), .mfhi(mfhi), .nop(tty),
    .mflo(mflo), .Is_RF(IsRF));
  BC_SELECTOR bc_selector_1 (
    .beq(beq), .bne(bne), .blez(blez), .bgtz(bgtz), .bltz(bltz), .jr(jr), .j(j), .BC_SELECTOR(BC_Select),
    .FLAG_CONDITION(BC_Flag));
  or or_5 (offsetSelect, andi, ori, xori);
  RF_INPUT_SELECTOR rf_input_selector_1 (
    .pop(pop), .lw(lw), .kbd(kbd), .rnd(rnd), .mfhi(mfhi), .mflo(mflo), .RF_INPUT_SELECTOR(InputToRF));
  Comparator #(.width(6)) comparator_17 (.a(Instruction_t), .b({6{1'b1}}), .eq(_11_1111));  // open: gt, lt
  nor nor_1 (nwrj, read, write, jump);
  and and_11 (slt, _00_0000, comparator_18_eq);
  Comparator #(.width(6)) comparator_18 (.a(Jump_Address[5:0]), .b(6'b101010), .eq(comparator_18_eq));  // open: gt, lt
  and and_12 (sltu, _00_0000, comparator_19_eq);
  Comparator #(.width(6)) comparator_19 (.a(Jump_Address[5:0]), .b(6'b101011), .eq(comparator_19_eq));  // open: gt, lt
  Comparator #(.width(6)) comparator_20 (.a(Instruction_t), .b(6'b001010), .eq(slti));  // open: gt, lt
  Comparator #(.width(6)) comparator_21 (.a(Instruction_t), .b(6'b001011), .eq(sltiu));  // open: gt, lt
  Comparator #(.width(6)) comparator_22 (.a(Jump_Address[5:0]), .b({6{1'b0}}), .eq(comparator_22_eq));  // open: gt, lt
  Comparator #(.width(6)) comparator_23 (.a(Jump_Address[5:0]), .b(6'b001000), .eq(comparator_23_eq));  // open: gt, lt
  Comparator #(.width(6)) comparator_24 (.a(Instruction_t), .b(6'b000100), .eq(beq));  // open: gt, lt
  Comparator #(.width(6)) comparator_25 (.a(Instruction_t), .b(6'b000101), .eq(bne));  // open: gt, lt
  Comparator #(.width(6)) comparator_26 (.a(Instruction_t), .b(6'b000110), .eq(blez));  // open: gt, lt
  Comparator #(.width(6)) comparator_27 (.a(Instruction_t), .b(6'b000111), .eq(bgtz));  // open: gt, lt
  Comparator #(.width(6)) comparator_28 (.a(Instruction_t), .b(6'b000001), .eq(bltz));  // open: gt, lt
  and and_13 (nop, _00_0000, comparator_22_eq);
  and and_14 (jr, _00_0000, comparator_23_eq);
  Comparator #(.width(6)) comparator_29 (.a(Instruction_t), .b(6'b000010), .eq(j));  // open: gt, lt
  Multiplexer #(.width(5), .enable("false")) multiplexer_1 (
    .in0(Jump_Address[15:11]), .in1(Jump_Address[20:16]), .out(dataAddress), .sel(Type_I));
  or or_6 (or_6_out, addi, slti, sltiu, offsetSelect, lw, sw);
  and and_15 (and_15_out, ~jr, BC_Select[0]);  // AND_Gate
  or or_7 (Type_I, or_6_out, and_15_out);
  Comparator #(.width(6)) comparator_30 (.a(Jump_Address[5:0]), .b({6{1'b0}}), .eq(comparator_30_eq));  // open: gt, lt
  Comparator #(.width(6)) comparator_31 (.a(Jump_Address[5:0]), .b(6'b000001), .eq(comparator_31_eq));  // open: gt, lt
  Comparator #(.width(6)) comparator_32 (.a(Instruction_t), .b(6'b100011), .eq(lw));  // open: gt, lt
  Comparator #(.width(6)) comparator_33 (.a(Instruction_t), .b(6'b101011), .eq(sw));  // open: gt, lt
  and and_16 (pop, _11_1000, comparator_30_eq);
  and and_17 (push, _11_1000, comparator_31_eq);
  Comparator #(.width(6)) comparator_34 (.a(Jump_Address[5:0]), .b(6'b010000), .eq(comparator_34_eq));  // open: gt, lt
  Comparator #(.width(6)) comparator_35 (.a(Jump_Address[5:0]), .b(6'b010010), .eq(comparator_35_eq));  // open: gt, lt
  and and_18 (mfhi, _00_0000, comparator_34_eq);
  and and_19 (mflo, _00_0000, comparator_35_eq);
  and and_20 (halt, _11_1111, comparator_36_eq);
  Comparator #(.width(6)) comparator_36 (.a(Jump_Address[5:0]), .b({6{1'b1}}), .eq(comparator_36_eq));  // open: gt, lt
  and and_21 (tty, _11_1111, comparator_37_eq);
  Comparator #(.width(6)) comparator_37 (.a(Jump_Address[5:0]), .b(6'b000001), .eq(comparator_37_eq));  // open: gt, lt
  and and_22 (rnd, _11_1111, comparator_38_eq);
  Comparator #(.width(6)) comparator_38 (.a(Jump_Address[5:0]), .b(6'b000010), .eq(comparator_38_eq));  // open: gt, lt
  and and_23 (kbd, _11_1111, comparator_39_eq);
  Comparator #(.width(6)) comparator_39 (.a(Jump_Address[5:0]), .b(6'b000100), .eq(comparator_39_eq));  // open: gt, lt

  assign offset = Jump_Address[15:0];
  assign Rs = Jump_Address[25:21];
  assign Rt = Jump_Address[20:16];

  // Other names for the same wires on the sheet: BC_Flag_Condition[2:0] = BC_Flag; DA[4:0] = dataAddress;
  //   InputToRFSelect[2:0] = InputToRF; INST = isInstr; Func_Code[5:0] = Jump_Address[5:0];
  //   Instruction_t[25:0] = Jump_Address; jmp_addr[25:0] = Jump_Address; Rd[4:0] = Jump_Address[15:11];
  //   Op_Code[5:0] = Instruction_t; isType_I = Type_I

  // Notes on the sheet:
  //   Read
  //   Write
  //   ARITHMETIC INSTRUCTIONS
  //   Jump
  //   INPUTS
  //   SELECTORS
  //   CONTROL UNIT FLAGS
  //   LOGICAL INSTRUCTIONS
  //   TYPE-I INSTRUCTIONS
  //   HI-LO
  //   TYPE-R INSTRUCTIONS
  //   OUTPUTS
  //   USE RF
  //   COMPARISON INSTRUCTIONS
  //   JUMP INSTRUCTIONS
  //   TYPE-J INSTRUCTION
  //   Is Type I
  //   DATA ADDRESS
  //   MEMORY INSTRUCTIONS
  //   REGISTER COPY INSTRUCTIONS
  //   REGISTER COPY INSTRUCTIONS
endmodule
