// Logisim project Program Counter.circ as structural Verilog: 1 circuit, main circuit Program Counter
module Program_Counter (
  input  [31:0] PC_in,
  input  Enable,
  input  Reset,
  input  Clock,
  output [31:0] PC_out
);

  Register #(.width(32)) register_1 (.D(PC_in), .en(Enable), .Q(PC_out), .clk(Clock), .clr(Reset));

  // Other names for the same wires on the sheet: CLK = Clock; EN = Enable; RST = Reset

  // Notes on the sheet:
  //   INPUTS
  //   OUTPUTS
endmodule
