// Logisim project RAM_ADDRESS.circ as structural Verilog: 1 circuit, main circuit RAM_ADDRESS
module RAM_ADDRESS (
  input  [31:0] ALU,
  input  [31:0] SP,
  input  [31:0] PC,
  input  [1:0] Selector,
  input  Push,
  output [31:0] RAM_Address
);

  wire [31:0] NewSP, subtractor_1_out;

  Subtractor #(.width(32)) subtractor_1 (.a(SP), .b(32'h4), .out(subtractor_1_out));  // open: bin, bout
  Multiplexer #(.width(32), .disabled(0), .enable("false")) multiplexer_1 (
    .in0(SP), .in1(subtractor_1_out), .out(NewSP), .sel(Push));
  Multiplexer #(.select(2), .width(32), .disabled(0), .enable("false")) multiplexer_2 (
    .in1(ALU), .in2(NewSP), .in3(PC), .out(RAM_Address));  // open: in0, sel

  // Other names for the same wires on the sheet: RA[31:0] = RAM_Address; SEL[1:0] = Selector

  // Notes on the sheet:
  //   INPUT
  //   OUTPUT
  //   STACK POINTER SELECTION
  //   RAM ADDRESS SELECTION
endmodule
