// Logisim project READ_RAM.circ as structural Verilog: 1 circuit, main circuit READ_RAM
module READ_RAM (
  input  [31:0] Bank_0,
  input  [31:0] RAM_Address,
  input  [3:0] Read_Time,
  input  [31:0] Bank_1,
  input  Clk,
  input  Rst,
  input  [31:0] Bank_2,
  input  Get,
  input  [31:0] Bank_3,
  output Ready,
  output [31:0] Data,
  output Chip_Sel
);

  wire demultiplexer_1_out0, demultiplexer_1_out1, or_1_out, or_2_out, TIMER;
  wire [31:0] multiplexer_1_out, reverse_1_data_reverse;

  or or_1 (or_1_out, demultiplexer_1_out0, Get);
  Register #(.width(1)) register_1 (.D(or_1_out), .Q(Chip_Sel), .clk(Clk), .clr(Rst));  // open: en
  Multiplexer #(.select(2), .width(32), .enable("false")) multiplexer_1 (
    .in0(Bank_0), .in1(Bank_1), .in2(Bank_2), .in3(Bank_3), .out(multiplexer_1_out), .sel(RAM_Address[3:2]));
  or or_2 (or_2_out, Ready, Rst);
  Demultiplexer #(.enable("false")) demultiplexer_1 (
    .out0(demultiplexer_1_out0), .out1(demultiplexer_1_out1), .in(Chip_Sel), .sel(TIMER));
  REVERSE reverse_1 (.Data_Input(multiplexer_1_out), .Data_Reverse(reverse_1_data_reverse));
  TIMER timer_1 (.Wait_Time(Read_Time), .Rst(or_2_out), .Clk(Clk), .Start(Chip_Sel), .Ready(TIMER));
  Register #(.width(32)) register_2 (.D(reverse_1_data_reverse), .en(Chip_Sel), .Q(Data), .clk(Clk), .clr(Rst));
  Register #(.width(1)) register_3 (.D(demultiplexer_1_out1), .Q(Ready), .clk(Clk), .clr(Rst));  // open: en

  // Other names for the same wires on the sheet: BANK0[31:0] = Bank_0; BANK1[31:0] = Bank_1; BANK2[31:0] = Bank_2;
  //   BANK3[31:0] = Bank_3; CS = Chip_Sel; SEL[1:0] = RAM_Address[3:2]; RD = Ready; RT[3:0] = Read_Time

  // Notes on the sheet:
  //   RAM BANKS
  //   INPUT
  //   READ DATA
  //   REVERSE RAM DATA
  //   TIMER
  //   RAM ADRESS
  //   AUXILIARS
  //   OUTPUT
endmodule
