// Logisim project REVERSE.circ as structural Verilog: 1 circuit, main circuit REVERSE
module REVERSE (
  input  [31:0] Data_Input,
  output [31:0] Data_Reverse
);


  assign Data_Reverse = {Data_Input[7:0], Data_Input[15:8], Data_Input[23:16], Data_Input[31:24]};
endmodule
