// Logisim project RF_INPUT.circ as structural Verilog: 1 circuit, main circuit RF_INPUT
module RF_INPUT (
  input  [31:0] RAM_Data,
  input  [6:0] Keyboard,
  input  [31:0] ALU_Output,
  input  [2:0] Selector,
  input  [31:0] HI,
  input  Clock,
  input  [31:0] LO,
  input  KBD_Available,
  output [31:0] RF_Input
);

  wire [31:0] KBD, KBD_IN, RAMDOM;

  Random #(.width(32), .trigger("falling")) RND (.clk(Clock), .out(RAMDOM));  // open: next, clr
  Multiplexer #(.width(32), .disabled(0), .enable("false")) multiplexer_1 (
    .in0({32{1'b1}}), .in1(KBD), .out(KBD_IN), .sel(KBD_Available));
  assign KBD = {{25{1'b0}}, Keyboard};  // Bit_Extender bit_extender_1
  Multiplexer #(.select(3), .width(32), .disabled(0), .enable("false")) multiplexer_2 (
    .in0(ALU_Output), .in1(KBD_IN), .in2(RAMDOM), .in3(RAM_Data), .in4(HI), .in5(LO), .out(RF_Input),
    .sel(Selector));  // open: in6, in7

  // Other names for the same wires on the sheet: ALU[31:0] = ALU_Output; CLK = Clock; KBD_AV = KBD_Available;
  //   RAM[31:0] = RAM_Data; RF_IN[31:0] = RF_Input; SEL[2:0] = Selector

  // Notes on the sheet:
  //   KEYBOARD INPUT
  //   RANDOM GENERATION
  //   INPUT
  //   RF INPUT SELECTION
  //   OUTUT
  //   SELECTION CODES
  //   000 - ALU
  //   001 - Keyboard
  //   010 - Random
  //   011 - RAM Data
  //   100 - HI
  //   101 - [LO]
endmodule
