// Logisim project RF_INPUT_SELECTOR.circ as structural Verilog: 1 circuit, main circuit RF_INPUT_SELECTOR
module RF_INPUT_SELECTOR (
  input  pop,
  input  [2:0] RF_INPUT_SELECTOR,
  input  lw,
  input  kbd,
  input  rnd,
  input  mfhi,
  input  mflo
);

  wire priority_encoder_1_gs, RAM;
  wire [2:0] priority_encoder_1_out;

  or or_1 (RAM, pop, lw);
  Priority_Encoder priority_encoder_1 (
    .in1(kbd), .in2(rnd), .in3(RAM), .in4(mfhi), .in5(mflo), .out(priority_encoder_1_out), .en_in(1'b1),
    .gs(priority_encoder_1_gs));  // open: in0, in6, in7, en_out
  Multiplexer #(.width(3), .disabled(0), .enable("false")) multiplexer_1 (
    .in0(3'b000), .in1(priority_encoder_1_out), .out(RF_INPUT_SELECTOR), .sel(priority_encoder_1_gs));

  // Other names for the same wires on the sheet: SELECTOR[2:0] = RF_INPUT_SELECTOR

  // Notes on the sheet:
  //   INPUTS
  //   KBD - 001
  //   RND - 010
  //   MFHI - 011
  //   MFLO - 100
  //   FLAG_CONDITION
  //   RAM
  //   OUTPUTS
  //   RF_SELECTOR_CODES
  //   RAM - 010
endmodule
