// Logisim project Register File.circ as structural Verilog: 1 circuit, main circuit Register File
module Register_File (
  input  [4:0] Data_Addr,
  input  push,
  input  pop,
  input  [31:0] DataInput,
  input  [4:0] SelectorA,
  input  [4:0] SelectorB,
  input  ReadWrite,
  input  Reset,
  input  PC_enable,
  input  Clock,
  output [31:0] RegisterA,
  output [31:0] RegisterB,
  output [31:0] Stack_Pointer
);

  wire F1, F2, F3, F4, F5, F6, F7, F8, F9, F10, F11, F12, F13, F14, F15, F16, F17, F18, F19, F20, F21, F22,
       F23, F24, F25, F26, F27, F28, F29, F30, F31, L31, or_1_out, or_2_out, or_3_out;
  wire [31:0] adder_1_out, multiplexer_3_out, multiplexer_5_out, Out0, Out1, Out2, Out3, Out4, Out5, Out6,
       Out7, Out8, Out9, Out10, Out11, Out12, Out13, Out14, Out15, Out16, Out17, Out18, Out19, Out20, Out21,
       Out22, Out23, Out24, Out25, Out26, Out27, Out28, Out29, Out30, Out31, SP, subtractor_1_out;

  Multiplexer #(.select(5), .width(32)) multiplexer_1 (
    .in0(Out0), .in1(Out1), .in2(Out2), .in3(Out3), .in4(Out4), .in5(Out5), .in6(Out6), .in7(Out7),
    .in8(Out8), .in9(Out9), .in10(Out10), .in11(Out11), .in12(Out12), .in13(Out13), .in14(Out14),
    .in15(Out15), .in16(Out16), .in17(Out17), .in18(Out18), .in19(Out19), .in20(Out20), .in21(Out21),
    .in22(Out22), .in23(Out23), .in24(Out24), .in25(Out25), .in26(Out26), .in27(Out27), .in28(Out28),
    .in29(Out29), .in30(Out30), .in31(Out31), .out(RegisterA), .sel(SelectorA));  // open: en
  Multiplexer #(.select(5), .width(32)) multiplexer_2 (
    .in0(Out0), .in1(Out1), .in2(Out2), .in3(Out3), .in4(Out4), .in5(Out5), .in6(Out6), .in7(Out7),
    .in8(Out8), .in9(Out9), .in10(Out10), .in11(Out11), .in12(Out12), .in13(Out13), .in14(Out14),
    .in15(Out15), .in16(Out16), .in17(Out17), .in18(Out18), .in19(Out19), .in20(Out20), .in21(Out21),
    .in22(Out22), .in23(Out23), .in24(Out24), .in25(Out25), .in26(Out26), .in27(Out27), .in28(Out28),
    .in29(Out29), .in30(Out30), .in31(Out31), .out(RegisterB), .sel(SelectorB));  // open: en
  Decoder #(.select(5), .disabled(0)) decoder_1 (
    .out1(F1), .out2(F2), .out3(F3), .out4(F4), .out5(F5), .out6(F6), .out7(F7), .out8(F8), .out9(F9),
    .out10(F10), .out11(F11), .out12(F12), .out13(F13), .out14(F14), .out15(F15), .out16(F16), .out17(F17),
    .out18(F18), .out19(F19), .out20(F20), .out21(F21), .out22(F22), .out23(F23), .out24(F24), .out25(F25),
    .out26(F26), .out27(F27), .out28(F28), .out29(F29), .out30(F30), .out31(F31), .sel(Data_Addr),
    .en(ReadWrite));  // open: out0
  Register #(.width(32), .trigger("falling")) R1 (.D(DataInput), .en(F1), .Q(Out1), .clk(Clock), .clr(Reset));
  Register #(.width(32), .trigger("falling")) R7 (.D(DataInput), .en(F7), .Q(Out7), .clk(Clock), .clr(Reset));
  Register #(.width(32), .trigger("falling")) R13 (.D(DataInput), .en(F13), .Q(Out13), .clk(Clock), .clr(Reset));
  Register #(.width(32), .trigger("falling")) R18 (.D(DataInput), .en(F18), .Q(Out18), .clk(Clock), .clr(Reset));
  Register #(.width(32), .trigger("falling")) R23 (.D(DataInput), .en(F23), .Q(Out23), .clk(Clock), .clr(Reset));
  Register #(.width(32), .trigger("falling")) R28 (.D(DataInput), .en(F28), .Q(Out28), .clk(Clock), .clr(Reset));
  Register #(.width(32), .trigger("falling")) R2 (.D(DataInput), .en(F2), .Q(Out2), .clk(Clock), .clr(Reset));
  Register #(.width(32), .trigger("falling")) R8 (.D(DataInput), .en(F8), .Q(Out8), .clk(Clock), .clr(Reset));
  Register #(.width(32), .trigger("falling")) R14 (.D(DataInput), .en(F14), .Q(Out14), .clk(Clock), .clr(Reset));
  Register #(.width(32), .trigger("falling")) R19 (.D(DataInput), .en(F19), .Q(Out19), .clk(Clock), .clr(Reset));
  Register #(.width(32), .trigger("falling")) R24 (.D(DataInput), .en(F24), .Q(Out24), .clk(Clock), .clr(Reset));
  Register #(.width(32), .trigger("falling")) R29 (.D(DataInput), .en(F29), .Q(Out29), .clk(Clock), .clr(Reset));
  Register #(.width(32), .trigger("falling")) R3 (.D(DataInput), .en(F3), .Q(Out3), .clk(Clock), .clr(Reset));
  Register #(.width(32), .trigger("falling")) R9 (.D(DataInput), .en(F9), .Q(Out9), .clk(Clock), .clr(Reset));
  Register #(.width(32), .trigger("falling")) R15 (.D(DataInput), .en(F15), .Q(Out15), .clk(Clock), .clr(Reset));
  Register #(.width(32), .trigger("falling")) R20 (.D(DataInput), .en(F20), .Q(Out20), .clk(Clock), .clr(Reset));
  Register #(.width(32), .trigger("falling")) R25 (.D(DataInput), .en(F25), .Q(Out25), .clk(Clock), .clr(Reset));
  Register #(.width(32), .trigger("falling")) R30 (.D(DataInput), .en(F30), .Q(Out30), .clk(Clock), .clr(Reset));
  Register #(.width(32), .trigger("falling")) R4 (.D(DataInput), .en(F4), .Q(Out4), .clk(Clock), .clr(Reset));
  Register #(.width(32), .trigger("falling")) R10 (.D(DataInput), .en(F10), .Q(Out10), .clk(Clock), .clr(Reset));
  Register #(.width(32), .trigger("falling")) R11 (.D(DataInput), .en(F11), .Q(Out11), .clk(Clock), .clr(Reset));
  Register #(.width(32), .trigger("falling")) R16 (.D(DataInput), .en(F16), .Q(Out16), .clk(Clock), .clr(Reset));
  Register #(.width(32), .trigger("falling")) R21 (.D(DataInput), .en(F21), .Q(Out21), .clk(Clock), .clr(Reset));
  Register #(.width(32), .trigger("falling")) R26 (.D(DataInput), .en(F26), .Q(Out26), .clk(Clock), .clr(Reset));
  Register #(.width(32), .trigger("falling")) R31 (.D(DataInput), .en(F31), .Q(Out31), .clk(Clock), .clr(Reset));
  Register #(.width(32), .trigger("falling")) R5 (.D(DataInput), .en(F5), .Q(Out5), .clk(Clock), .clr(Reset));
  or or_1 (or_1_out, push, F31, pop);
  or or_2 (or_2_out, F31, PC_enable);
  Subtractor #(.width(32)) subtractor_1 (.a(Stack_Pointer), .b(32'h4), .out(subtractor_1_out));  // open: bin, bout
  Adder #(.width(32)) adder_1 (.a(32'h4), .b(Stack_Pointer), .out(adder_1_out));  // open: cin, cout
  Register #(.width(32), .trigger("falling")) R12 (.D(DataInput), .en(F12), .Q(Out12), .clk(Clock), .clr(Reset));
  Register #(.width(32), .trigger("falling")) R17 (.D(DataInput), .en(F17), .Q(Out17), .clk(Clock), .clr(Reset));
  Register #(.width(32), .trigger("falling")) R22 (.D(DataInput), .en(F22), .Q(Out22), .clk(Clock), .clr(Reset));
  Register #(.width(32), .trigger("falling")) R27 (.D(DataInput), .en(F27), .Q(Out27), .clk(Clock), .clr(Reset));
  Register #(.width(32), .trigger("falling")) R0 (.D(DataInput), .en(1'b0), .Q(Out0), .clk(Clock), .clr(Reset));
  and and_1 (L31, or_1_out, or_2_out);
  Multiplexer #(.width(32), .enable("false")) multiplexer_3 (
    .in0(subtractor_1_out), .in1(adder_1_out), .out(multiplexer_3_out), .sel(pop));
  Register #(.width(32), .trigger("falling")) R6 (.D(DataInput), .en(F6), .Q(Out6), .clk(Clock), .clr(Reset));
  Multiplexer #(.width(32), .enable("false")) multiplexer_4 (
    .in0(multiplexer_3_out), .in1({32{1'b1}}), .out(SP), .sel(Reset));
  Multiplexer #(.width(32), .enable("false")) multiplexer_5 (
    .in0(SP), .in1(DataInput), .out(multiplexer_5_out), .sel(F31));
  or or_3 (or_3_out, L31, Reset);
  Register #(.width(32)) u_SP (.D(multiplexer_5_out), .en(or_3_out), .Q(Stack_Pointer), .clk(Clock));  // open: clr

  // Other names for the same wires on the sheet: CLK = Clock; DA[4:0] = Data_Addr; DI[31:0] = DataInput;
  //   OutA[31:0] = RegisterA; OutB[31:0] = RegisterB; Q31[31:0] = Stack_Pointer; Rst = Reset; RW = ReadWrite;
  //   SA[4:0] = SelectorA; SB[4:0] = SelectorB

  // Notes on the sheet:
  //   INPUTS
  //   DECODER
  //   OUTPUTS
  //   REGISTERS
endmodule
