// Logisim project TIMER.circ as structural Verilog: 1 circuit, main circuit TIMER
module TIMER (
  input  [3:0] Wait_Time,
  input  Rst,
  input  Clk,
  input  Start,
  output Ready
);

  wire [3:0] PASSED;

  Comparator #(.width(4)) comparator_1 (.a(PASSED), .b(Wait_Time), .eq(Ready));  // open: gt, lt
  Counter #(.width(4), .max('hf)) counter_1 (.count(Start), .Q(PASSED), .clk(Clk), .clr(Rst));  // open: load, D, carry

  // Other names for the same wires on the sheet: WT[3:0] = Wait_Time

  // Notes on the sheet:
  //   INPUT
  //   COUNT PASSED TIME
  //   OUTPUT
endmodule
