// Logisim project WRITE_RAM.circ as structural Verilog: 1 circuit, main circuit WRITE_RAM
module WRITE_RAM (
  input  [31:0] Data,
  input  [31:0] RAM_Address,
  input  [3:0] Write_Time,
  input  Clk,
  input  Rst,
  input  Write,
  output [31:0] Bank_0,
  output Ready,
  output [31:0] Bank_1,
  output [31:0] Bank_2,
  output Chip_Sel,
  output [31:0] Bank_3
);

  wire demultiplexer_2_out0, demultiplexer_2_out1, or_1_out, or_2_out, TIMER;
  wire [31:0] reverse_1_data_reverse;

  or or_1 (or_1_out, demultiplexer_2_out0, Write);
  Register #(.width(1)) register_1 (.D(or_1_out), .Q(Chip_Sel), .clk(Clk), .clr(Rst));  // open: en
  REVERSE reverse_1 (.Data_Input(Data), .Data_Reverse(reverse_1_data_reverse));
  Demultiplexer #(.select(2), .width(32), .disabled(0), .enable("false")) demultiplexer_1 (
    .out0(Bank_0), .out1(Bank_1), .out2(Bank_2), .out3(Bank_3), .in(reverse_1_data_reverse),
    .sel(RAM_Address[3:2]));
  or or_2 (or_2_out, Ready, Rst);
  Demultiplexer #(.enable("false")) demultiplexer_2 (
    .out0(demultiplexer_2_out0), .out1(demultiplexer_2_out1), .in(Chip_Sel), .sel(TIMER));
  TIMER timer_1 (.Wait_Time(Write_Time), .Rst(or_2_out), .Clk(Clk), .Start(Chip_Sel), .Ready(TIMER));
  Register #(.width(1)) register_2 (.D(demultiplexer_2_out1), .Q(Ready), .clk(Clk), .clr(Rst));  // open: en

  // Other names for the same wires on the sheet: BANK0[31:0] = Bank_0; BANK1[31:0] = Bank_1; BANK2[31:0] = Bank_2;
  //   BANK3[31:0] = Bank_3; CS = Chip_Sel; SEL[1:0] = RAM_Address[3:2]; RW = Ready; WT[3:0] = Write_Time

  // Notes on the sheet:
  //   INPUT
  //   AUXILIARS
  //   WRITE DATA
  //   REVERSE RAM DATA
  //   TIMER
  //   OUTPUT
endmodule
