// Logisim project s-mips.circ as structural Verilog: 6 circuits, main circuit S-MIPS Board
module S_MIPS_Board (
  input  DESHABILITAR_DISPATCHER,
  output halt
);

  wire button_1_out, CLK, CS, d_ff_1_q, LCLR, LoadRAM, LoadRAMOn, LW, R_R_W, R_W, ram_dispatcher_1_finished,
       RCS, Reset_out, RST, TTY_EN;
  wire [2:0] KDB;
  wire [3:0] LMask, Mask, ram_1_read_time, ram_1_write_time, RMask;
  wire [6:0] KDB_DATA, TTY_DATA;
  wire [15:0] Addr, LAddr, RAddr;
  wire [31:0] I0, I1, I2, I3, LData, ram_1_data_out_0, ram_1_data_out_1, ram_1_data_out_2, ram_1_data_out_3,
       RI0, RI1, RI2, RI3;

  TTY #(.rows(25), .cols(80)) tty_1 (.data(TTY_DATA), .clk(CLK), .we(TTY_EN), .clr(RST));
  not not_1 (LoadRAMOn, ram_dispatcher_1_finished);
  RAM_Dispatcher ram_dispatcher_1 (
    .WriteTime(ram_1_write_time), .Clock(CLK), .Data(LData), .Address(LAddr), .Mask(LMask),
    .Finished(ram_dispatcher_1_finished), .Write(LW), .CLR(LCLR));
  Keyboard #(.buflen(64)) keyboard_1 (.clk(CLK), .re(KDB[0]), .avail(KDB[2]), .data(KDB_DATA));  // open: clr
  RAM ram_1 (
    .Address(RAddr), .Data_Out_0(ram_1_data_out_0), .Data_Out_1(ram_1_data_out_1),
    .Data_Out_2(ram_1_data_out_2), .Data_Out_3(ram_1_data_out_3), .Data_In_0(RI0), .Data_In_1(RI1),
    .Data_In_2(RI2), .Data_In_3(RI3), .Mask(RMask), .nRead_Write(R_R_W), .Chip_Select(RCS),
    .Read_Time(ram_1_read_time), .Reset(button_1_out), .Write_Time(ram_1_write_time));
  Button button_1 (.out(button_1_out));
  D_Flip_Flop d_ff_1 (.clk(CLK), .D(1'b1), .Q(d_ff_1_q), .reset(Reset_out));  // open: Qn, preset, en
  Button Reset (.out(Reset_out));
  S_MIPS s_mips_1 (
    .Kbd_Enable(KDB[0]), .Address(Addr), .Kbd_Clear(KDB[1]), .Kbd_Available(KDB[2]), .RAM_In_0(I0),
    .Kbd_ASCII_Data(KDB_DATA), .RAM_In_1(I1), .TTY_Enable(TTY_EN), .RAM_In_2(I2), .RAM_In_3(I3),
    .TTY_ASCII_Data(TTY_DATA), .Reset(RST), .RAM_Out_0(ram_1_data_out_0), .Clock(CLK),
    .RAM_Out_1(ram_1_data_out_1), .Stop(halt), .RAM_Out_2(ram_1_data_out_2), .RAM_Out_3(ram_1_data_out_3),
    .Mask(Mask), .Read_Time(ram_1_read_time), .Write_Time(ram_1_write_time), .nRead_Write(R_W),
    .Chip_Select(CS));
  D_Flip_Flop d_ff_2 (.clk(CLK), .D(d_ff_1_q), .Qn(LCLR), .reset(Reset_out));  // open: Q, preset, en
  or or_1 (RST, LCLR, LoadRAM);
  Clock clock_1 (.out(CLK));
  Multiplexer #(.width(32), .enable("false")) multiplexer_1 (.in0(I0), .in1(LData), .out(RI0), .sel(LoadRAM));
  Multiplexer #(.width(32), .enable("false")) multiplexer_2 (.in0(I1), .in1(LData), .out(RI1), .sel(LoadRAM));
  Multiplexer #(.width(32), .enable("false")) multiplexer_3 (.in0(I2), .in1(LData), .out(RI2), .sel(LoadRAM));
  Multiplexer #(.width(32), .enable("false")) multiplexer_4 (.in0(I3), .in1(LData), .out(RI3), .sel(LoadRAM));
  and and_1 (LoadRAM, ~DESHABILITAR_DISPATCHER, LoadRAMOn);  // AND_Gate
  Multiplexer #(.width(16), .enable("false")) multiplexer_5 (.in0(Addr), .in1(LAddr), .out(RAddr), .sel(LoadRAM));
  Multiplexer #(.width(4), .enable("false")) multiplexer_6 (.in0(Mask), .in1(LMask), .out(RMask), .sel(LoadRAM));
  Multiplexer #(.enable("false")) multiplexer_7 (.in0(CS), .in1(LW), .out(RCS), .sel(LoadRAM));
  Multiplexer #(.enable("false")) multiplexer_8 (.in0(R_W), .in1(LW), .out(R_R_W), .sel(LoadRAM));

  // Notes on the sheet:
  //   NO MODIFICAR
  //   Keyboard
endmodule

module RAM (
  input  [15:0] Address,
  input  [31:0] Data_In_0,
  input  [31:0] Data_In_1,
  input  [31:0] Data_In_2,
  input  [31:0] Data_In_3,
  input  [3:0] Mask,
  input  nRead_Write,
  input  Chip_Select,
  input  Reset,
  output [31:0] Data_Out_0,
  output [31:0] Data_Out_1,
  output [31:0] Data_Out_2,
  output [31:0] Data_Out_3,
  output [3:0] Read_Time,
  output [3:0] Write_Time
);

  wire and_2_out, and_3_out, and_4_out, and_5_out, and_6_out, and_7_out, and_8_out, and_9_out, Changed, CLK,
       comparator_2_eq, comparator_3_eq, comparator_4_eq, comparator_5_eq, comparator_6_eq, Count,
       demultiplexer_3_out0, Idle, Idle_q, Load, Load0, Load1, nand_1_out, or_1_out, or_2_out, or_3_out,
       or_4_out, or_5_out, or_6_out, or_7_out, or_8_out, or_9_out, or_10_out, Proc_q, Update_Mem, Zero_Time;
  wire [3:0] counter_1_q, multiplexer_1_out, subtractor_1_out;
  wire [31:0] register_1_q, register_2_q, register_3_q, register_4_q, register_5_q;

  // Probe on 4'b0011
  // Probe on 4'b0010
  Multiplexer #(.width(4), .enable("false")) multiplexer_1 (
    .in0(4'b0011), .in1(4'b0010), .out(multiplexer_1_out), .sel(nRead_Write));
  or or_1 (or_1_out, Idle, Update_Mem);
  or or_2 (or_2_out, ~Chip_Select, Reset);  // OR_Gate
  Subtractor #(.width(4)) subtractor_1 (.a(multiplexer_1_out), .b(4'b0010), .out(subtractor_1_out));  // open: bin, bout
  Demultiplexer #(.enable("false")) demultiplexer_1 (.out0(Idle), .out1(Load0), .in(Idle_q), .sel(Changed));
  D_Flip_Flop u_Idle (.clk(CLK), .D(or_1_out), .Q(Idle_q), .preset(or_2_out));  // open: Qn, en, reset
  // Probe on counter_1_q
  Counter #(.width(4), .max('hf)) counter_1 (
    .load(Load), .D(subtractor_1_out), .count(Count), .Q(counter_1_q), .clk(CLK), .clr(or_3_out));  // open: carry
  or or_3 (or_3_out, ~Chip_Select, Reset);  // OR_Gate
  Comparator #(.width(4), .mode("unsigned")) comparator_1 (
    .a(4'b0000), .b(counter_1_q), .eq(Zero_Time));  // open: gt, lt
  or or_4 (or_4_out, Count, Load0, Load1);
  Register #(.width(32)) register_1 (.D(Data_In_0), .en(Chip_Select), .Q(register_1_q), .clk(CLK), .clr(or_5_out));
  or or_5 (or_5_out, ~Chip_Select, Reset);  // OR_Gate
  Register #(.width(32)) register_2 (.D(Data_In_1), .en(Chip_Select), .Q(register_2_q), .clk(CLK), .clr(or_6_out));
  or or_6 (or_6_out, ~Chip_Select, Reset);  // OR_Gate
  Register #(.width(32)) register_3 (.D(Data_In_2), .en(Chip_Select), .Q(register_3_q), .clk(CLK), .clr(or_7_out));
  or or_7 (or_7_out, ~Chip_Select, Reset);  // OR_Gate
  Register #(.width(32)) register_4 (.D(Data_In_3), .en(Chip_Select), .Q(register_4_q), .clk(CLK), .clr(or_8_out));
  or or_8 (or_8_out, ~Chip_Select, Reset);  // OR_Gate
  Register #(.width(32)) register_5 (
    .D({{11{1'b1}}, nRead_Write, Mask, Address}), .en(Chip_Select), .Q(register_5_q), .clk(CLK),
    .clr(or_9_out));
  or or_9 (or_9_out, ~Chip_Select, Reset);  // OR_Gate
  D_Flip_Flop Proc (.clk(CLK), .D(or_4_out), .Q(Proc_q), .reset(or_10_out));  // open: Qn, preset, en
  or or_10 (or_10_out, ~Chip_Select, Reset);  // OR_Gate
  Demultiplexer #(.enable("false")) demultiplexer_2 (
    .out0(Count), .out1(Update_Mem), .in(demultiplexer_3_out0), .sel(Zero_Time));
  Demultiplexer #(.enable("false")) demultiplexer_3 (
    .out0(demultiplexer_3_out0), .out1(Load1), .in(Proc_q), .sel(Changed));
  Clock clock_1 (.out(CLK));
  Comparator #(.width(32)) comparator_2 (.a(register_1_q), .b(Data_In_0), .eq(comparator_2_eq));  // open: gt, lt
  Comparator #(.width(32)) comparator_3 (.a(register_2_q), .b(Data_In_1), .eq(comparator_3_eq));  // open: gt, lt
  Comparator #(.width(32)) comparator_4 (.a(register_3_q), .b(Data_In_2), .eq(comparator_4_eq));  // open: gt, lt
  Comparator #(.width(32)) comparator_5 (.a(register_4_q), .b(Data_In_3), .eq(comparator_5_eq));  // open: gt, lt
  Comparator #(.width(32)) comparator_6 (
    .a(register_5_q), .b({{11{1'b1}}, nRead_Write, Mask, Address}), .eq(comparator_6_eq));  // open: gt, lt
  nand nand_1 (nand_1_out, comparator_6_eq, comparator_2_eq, comparator_3_eq, comparator_4_eq, comparator_5_eq);
  and and_1 (Changed, nand_1_out, Chip_Select);
  or or_11 (Load, Count, Load1, Load0);
  and and_2 (and_2_out, Mask[0], Update_Mem, nRead_Write);
  and and_3 (and_3_out, Mask[1], Update_Mem, nRead_Write);
  and and_4 (and_4_out, Mask[2], Update_Mem, nRead_Write);
  and and_5 (and_5_out, Mask[3], Update_Mem, nRead_Write);
  RAM_part #(.addrWidth(16), .dataWidth(32), .bus("separate")) ram_1 (
    .addr(Address), .din(Data_In_0), .data(Data_Out_0), .str(and_2_out), .sel(Chip_Select), .clk(CLK),
    .ld(and_6_out), .clr(Reset));
  and and_6 (and_6_out, ~nRead_Write, Idle);  // AND_Gate
  RAM_part #(.addrWidth(16), .dataWidth(32), .bus("separate")) ram_2 (
    .addr(Address), .din(Data_In_1), .data(Data_Out_1), .str(and_3_out), .sel(Chip_Select), .clk(CLK),
    .ld(and_7_out), .clr(Reset));
  and and_7 (and_7_out, ~nRead_Write, Idle);  // AND_Gate
  RAM_part #(.addrWidth(16), .dataWidth(32), .bus("separate")) ram_3 (
    .addr(Address), .din(Data_In_2), .data(Data_Out_2), .str(and_4_out), .sel(Chip_Select), .clk(CLK),
    .ld(and_8_out), .clr(Reset));
  and and_8 (and_8_out, ~nRead_Write, Idle);  // AND_Gate
  RAM_part #(.addrWidth(16), .dataWidth(32), .bus("separate")) ram_4 (
    .addr(Address), .din(Data_In_3), .data(Data_Out_3), .str(and_5_out), .sel(Chip_Select), .clk(CLK),
    .ld(and_9_out), .clr(Reset));
  and and_9 (and_9_out, ~nRead_Write, Idle);  // AND_Gate

  assign Read_Time = 4'b0011;
  assign Write_Time = 4'b0010;

  // Other names for the same wires on the sheet: M0 = Mask[0]; M1 = Mask[1]; M2 = Mask[2]; M3 = Mask[3];
  //   RW = nRead_Write; CLR = Reset; CS = Chip_Select; Load2 = Count

  // Notes on the sheet:
  //   NO MODIFICAR
  //   excepto quizás los valores RT y WT
  //   BANK0
  //   BANK1
  //   BANK2
  //   BANK3
endmodule

module S_MIPS (
  input  Kbd_Available,
  input  [6:0] Kbd_ASCII_Data,
  input  [31:0] RAM_Out_0,
  input  [31:0] RAM_Out_1,
  input  Reset,
  input  [31:0] RAM_Out_2,
  input  Clock,
  input  [31:0] RAM_Out_3,
  input  [3:0] Read_Time,
  input  [3:0] Write_Time,
  output Kbd_Enable,
  output [15:0] Address,
  output Kbd_Clear,
  output TTY_Enable,
  output [6:0] TTY_ASCII_Data,
  output Stop,
  output [31:0] RAM_In_0,
  output [31:0] RAM_In_1,
  output [31:0] RAM_In_2,
  output [31:0] RAM_In_3,
  output [3:0] Mask,
  output nRead_Write,
  output Chip_Select
);

  wire HALT, HI_LO, HI_LO_EN, INS_EN, ISINST, ISREAD, ISRF, ISWRITE, JMP, KBD, OFFSEL, PC_EN, POP, PUSH,
       READ, RF_EN, RND, RREAD, RWRITE, SW, TTY, TYPEI, WRITE;
  wire [1:0] BCSEL, MAS;
  wire [2:0] BCFLAG, RFSEL;
  wire [3:0] ALUOP;
  wire [4:0] DA, RS, RT;
  wire [15:0] OFFSET;
  wire [25:0] JMPADR;
  wire [31:0] ALU, branch_control_1_nia, DATAIN, DATAOU, INS, PC, PC_OUT, RAM_AD, RS_t, RT_t, SP;

  RAM_ADDRESS ram_address_1 (.ALU(ALU), .SP(SP), .PC(PC), .Selector(MAS), .Push(PUSH), .RAM_Address(RAM_AD));
  Instruction_Decoder instruction_decoder_1 (
    .Instruction(INS), .Write_Instr(INS_EN), .Rs(RS), .read(ISREAD), .InputToRF(RFSEL), .push(PUSH),
    .kbd(KBD), .offsetSelect(OFFSEL), .Rt(RT), .write(ISWRITE), .BC_Select(BCSEL), .pop(POP), .HI_LO(HI_LO),
    .halt(HALT), .sw(SW), .BC_Flag(BCFLAG), .Jump_Address(JMPADR), .ALU_Op(ALUOP), .tty(TTY),
    .dataAddress(DA), .jump(JMP), .rnd(RND), .offset(OFFSET), .MemAddrSelect(MAS), .IsRF(ISRF),
    .Type_I(TYPEI), .Clck(Clock), .Rst(Reset), .isInstr(ISINST));
  BRANCH_CONTROL branch_control_1 (
    .RS(RS_t), .JS(JMPADR), .RT(RT_t), .Offset(OFFSET), .Branch_Selector(BCSEL), .IA(PC_OUT),
    .Flag_Condition(BCFLAG), .NIA(branch_control_1_nia));
  // DATA_PATH data_path_1: pin names not known; wires that end beside it: POP, PUSH, RF_EN, TYPEI, Kbd_Available, SW, PC_EN, OFFSEL, HI_LO_EN, DATAOU, Reset, OFFSET, Clock, Kbd_ASCII_Data, RS, DA, RT, RFSEL, DATAIN, RS_t, RT_t, SP, ALU, TTY_ASCII_Data, ALUOP
  RAM_ACCESS ram_access_1 (
    .RAM_Output_0(RAM_Out_0), .Data_Input(DATAIN), .RAM_Adress(RAM_AD), .RAM_Output_1(RAM_Out_1),
    .Read_Time(Read_Time), .RAM_Output_2(RAM_Out_2), .Write_Time(Write_Time), .RAM_Output_3(RAM_Out_3),
    .Clk(Clock), .Write(WRITE), .Rst(Reset), .Read(READ), .RAM_Input_0(RAM_In_3), .Data_Output(DATAOU),
    .RAM_Input_1(RAM_In_3), .Address(Address), .Mask(Mask), .RAM_Input_2(RAM_In_3), .CS(Chip_Select),
    .R_W(nRead_Write), .Ready_Read(RREAD), .RAM_Input_3(RAM_In_3), .Ready_Write(RWRITE));
  Program_Counter program_counter_1 (
    .PC_in(branch_control_1_nia), .PC_out(PC_OUT), .Enable(PC_EN), .Reset(Reset), .Clock(Clock));
  Control_Unit control_unit_1 (
    .CLK(Clock), .ready_to_read(RREAD), .fetch_data(READ), .kbd_enable(Kbd_Enable), .RST(Reset),
    .ready_to_write(RWRITE), .write_data(WRITE), .\end (Stop), .isRF(ISRF), .halt(HALT), .PC_enable(PC_EN),
    .HI_LO_enable(HI_LO_EN), .isJmp(JMP), .is_kbd(KBD), .RF_enable(RF_EN), .is_instruction(ISINST),
    .isRead(ISREAD), .is_tty(TTY), .Instruction_Memory_enable(INS_EN), .HI_LO(HI_LO), .isWrite(ISWRITE),
    .tty_enable(TTY_Enable));

  assign Kbd_Clear = Reset;

  // Other names for the same wires on the sheet: CLK = Clock; CS = Chip_Select; KBD_AVAIL = Kbd_Available;
  //   CLR = Reset; KBD_CLR = Reset; KBD_DATA[6:0] = Kbd_ASCII_Data; RAM_A[15:0] = Address;
  //   RAM_INPUT_0[31:0] = RAM_In_0; RAM_INPUT_1[31:0] = RAM_In_1; RAM_INPUT_2[31:0] = RAM_In_2;
  //   RAM_INPUT_3[31:0] = RAM_In_3; RAM_MASK[3:0] = Mask; RAM_OUTPUT_0[31:0] = RAM_Out_0;
  //   RAM_OUTPUT_1[31:0] = RAM_Out_1; RAM_OUTPUT_2[31:0] = RAM_Out_2; RAM_OUTPUT_3[31:0] = RAM_Out_3;
  //   RW = nRead_Write; TTY_DATA[6:0] = TTY_ASCII_Data

  // Notes on the sheet:
  //   RAM ADDRESS
  //   DATA FROM RAM
  //   DATA TO RAM
  //   DATA WRITE MASK
  //   RAM TIMING
  //   RAM CONTROL
  //   KEYBOARD
  //   TTY
  //   SEQUENCING
  //   INSTRUCTION SECTION
  //   RAM SECTION
  //   BRANCH CONTROL AND PROGRAM COUNTER SECTION
  //   DATA PATH SECTION
  //   CONTROL UNIT SECTION
endmodule

module RAM_Dispatcher (
  input  [3:0] WriteTime,
  input  Clock,
  input  CLR,
  output [31:0] Data,
  output [15:0] Address,
  output [3:0] Mask,
  output Finished,
  output Write
);

  wire demultiplexer_2_out1, demultiplexer_3_out1, End, IDLE_q, IncAddr, Load, or_1_out, or_2_out, While_q,
       WriteEnd;
  wire [3:0] counter_1_q;
  wire [31:0] CurrentAddress_q;

  Counter #(.width(32), .max('hffffffff)) CurrentAddress (
    .count(IncAddr), .Q({CurrentAddress_q[31:18], Address, CurrentAddress_q[1:0]}), .clk(Clock), .clr(CLR));  // open: load, D, carry
  or or_1 (or_1_out, IncAddr, demultiplexer_3_out1, Finished);
  D_Flip_Flop IDLE (.clk(Clock), .D(or_1_out), .Q(IDLE_q), .preset(CLR));  // open: Qn, en, reset
  Demultiplexer #(.enable("false")) demultiplexer_1 (.out0(Load), .out1(Finished), .in(IDLE_q), .sel(End));
  D_Flip_Flop While (.clk(Clock), .D(or_2_out), .Q(While_q), .reset(CLR));  // open: Qn, preset, en
  or or_2 (or_2_out, Write, Load);
  RAM_part #(.addrWidth(18), .dataWidth(32)) ram_1 (
    .addr({Address, CurrentAddress_q[1:0]}), .data(Data), .clk(Clock));  // open: sel, ld, clr
  Demultiplexer #(.enable("false")) demultiplexer_2 (
    .out0(Write), .out1(demultiplexer_2_out1), .in(While_q), .sel(WriteEnd));
  Decoder #(.select(2)) decoder_1 (
    .out0(Mask[0]), .out1(Mask[1]), .out2(Mask[2]), .out3(Mask[3]), .sel(CurrentAddress_q[1:0]));  // open: en
  Demultiplexer #(.enable("false")) demultiplexer_3 (
    .out0(IncAddr), .out1(demultiplexer_3_out1), .in(demultiplexer_2_out1), .sel(End));
  Counter #(.width(4), .max('hf)) counter_1 (
    .load(Load), .D(WriteTime), .count(Write), .Q(counter_1_q), .clk(Clock));  // open: carry, clr
  Comparator #(.width(32)) comparator_1 (.a(Data), .b({32{1'b1}}), .eq(End));  // open: gt, lt
  Comparator #(.width(4)) comparator_2 (.a(4'b0000), .b(counter_1_q), .eq(WriteEnd));  // open: gt, lt

  // Other names for the same wires on the sheet: CLK = Clock; Count = Write; WT[3:0] = WriteTime
endmodule

module Register_File (
  input  [4:0] Data_Addr,
  input  [31:0] DataInput,
  input  [4:0] SelectorA,
  input  [4:0] SelectorB,
  input  ReadWrite,
  input  Reset,
  input  Clock,
  output [31:0] RegisterA,
  output [31:0] RegisterB
);

  wire F1, F2, F3, F4, F5, F6, F7, F8, F9, F10, F11, F12, F13, F14, F15, F16, F17, F18, F19, F20, F21, F22,
       F23, F24, F25, F26, F27, F28, F29, F30, F31;
  wire [31:0] Out0, Out1, Out2, Out3, Out4, Out5, Out6, Out7, Out8, Out9, Out10, Out11, Out12, Out13, Out14,
       Out15, Out16, Out17, Out18, Out19, Out20, Out21, Out22, Out23, Out24, Out25, Out26, Out27, Out28,
       Out29, Out30, Out31;

  Multiplexer #(.select(5), .width(32)) multiplexer_1 (
    .in0(Out0), .in1(Out1), .in2(Out2), .in3(Out3), .in4(Out4), .in5(Out5), .in6(Out6), .in7(Out7),
    .in8(Out8), .in9(Out9), .in10(Out10), .in11(Out11), .in12(Out12), .in13(Out13), .in14(Out14),
    .in15(Out15), .in16(Out16), .in17(Out17), .in18(Out18), .in19(Out19), .in20(Out20), .in21(Out21),
    .in22(Out22), .in23(Out23), .in24(Out24), .in25(Out25), .in26(Out26), .in27(Out27), .in28(Out28),
    .in29(Out29), .in30(Out30), .in31(Out31), .out(RegisterA), .sel(SelectorA));  // open: en
  Multiplexer #(.select(5), .width(32)) multiplexer_2 (
    .in0(Out0), .in1(Out1), .in2(Out2), .in3(Out3), .in4(Out4), .in5(Out5), .in6(Out6), .in7(Out7),
    .in8(Out8), .in9(Out9), .in10(Out10), .in11(Out11), .in12(Out12), .in13(Out13), .in14(Out14),
    .in15(Out15), .in16(Out16), .in17(Out17), .in18(Out18), .in19(Out19), .in20(Out20), .in21(Out21),
    .in22(Out22), .in23(Out23), .in24(Out24), .in25(Out25), .in26(Out26), .in27(Out27), .in28(Out28),
    .in29(Out29), .in30(Out30), .in31(Out31), .out(RegisterB), .sel(SelectorB));  // open: en
  Decoder #(.select(5)) decoder_1 (
    .out1(F1), .out2(F2), .out3(F3), .out4(F4), .out5(F5), .out6(F6), .out7(F7), .out8(F8), .out9(F9),
    .out10(F10), .out11(F11), .out12(F12), .out13(F13), .out14(F14), .out15(F15), .out16(F16), .out17(F17),
    .out18(F18), .out19(F19), .out20(F20), .out21(F21), .out22(F22), .out23(F23), .out24(F24), .out25(F25),
    .out26(F26), .out27(F27), .out28(F28), .out29(F29), .out30(F30), .out31(F31), .sel(Data_Addr),
    .en(ReadWrite));  // open: out0
  Register #(.width(32), .trigger("falling")) R1 (.D(DataInput), .en(F1), .Q(Out1), .clk(Clock), .clr(Reset));
  Register #(.width(32), .trigger("falling")) R7 (.D(DataInput), .en(F7), .Q(Out7), .clk(Clock), .clr(Reset));
  Register #(.width(32), .trigger("falling")) R13 (.D(DataInput), .en(F13), .Q(Out13), .clk(Clock), .clr(Reset));
  Register #(.width(32), .trigger("falling")) R18 (.D(DataInput), .en(F18), .Q(Out18), .clk(Clock), .clr(Reset));
  Register #(.width(32), .trigger("falling")) R23 (.D(DataInput), .en(F23), .Q(Out23), .clk(Clock), .clr(Reset));
  Register #(.width(32), .trigger("falling")) R28 (.D(DataInput), .en(F28), .Q(Out28), .clk(Clock), .clr(Reset));
  Register #(.width(32), .trigger("falling")) R2 (.D(DataInput), .en(F2), .Q(Out2), .clk(Clock), .clr(Reset));
  Register #(.width(32), .trigger("falling")) R8 (.D(DataInput), .en(F8), .Q(Out8), .clk(Clock), .clr(Reset));
  Register #(.width(32), .trigger("falling")) R14 (.D(DataInput), .en(F14), .Q(Out14), .clk(Clock), .clr(Reset));
  Register #(.width(32), .trigger("falling")) R19 (.D(DataInput), .en(F19), .Q(Out19), .clk(Clock), .clr(Reset));
  Register #(.width(32), .trigger("falling")) R24 (.D(DataInput), .en(F24), .Q(Out24), .clk(Clock), .clr(Reset));
  Register #(.width(32), .trigger("falling")) R29 (.D(DataInput), .en(F29), .Q(Out29), .clk(Clock), .clr(Reset));
  Register #(.width(32), .trigger("falling")) R3 (.D(DataInput), .en(F3), .Q(Out3), .clk(Clock), .clr(Reset));
  Register #(.width(32), .trigger("falling")) R9 (.D(DataInput), .en(F9), .Q(Out9), .clk(Clock), .clr(Reset));
  Register #(.width(32), .trigger("falling")) R15 (.D(DataInput), .en(F15), .Q(Out15), .clk(Clock), .clr(Reset));
  Register #(.width(32), .trigger("falling")) R20 (.D(DataInput), .en(F20), .Q(Out20), .clk(Clock), .clr(Reset));
  Register #(.width(32), .trigger("falling")) R25 (.D(DataInput), .en(F25), .Q(Out25), .clk(Clock), .clr(Reset));
  Register #(.width(32), .trigger("falling")) R30 (.D(DataInput), .en(F30), .Q(Out30), .clk(Clock), .clr(Reset));
  Register #(.width(32), .trigger("falling")) R4 (.D(DataInput), .en(F4), .Q(Out4), .clk(Clock), .clr(Reset));
  Register #(.width(32), .trigger("falling")) R10 (.D(DataInput), .en(F10), .Q(Out10), .clk(Clock), .clr(Reset));
  Register #(.width(32), .trigger("falling")) R11 (.D(DataInput), .en(F11), .Q(Out11), .clk(Clock), .clr(Reset));
  Register #(.width(32), .trigger("falling")) R16 (.D(DataInput), .en(F16), .Q(Out16), .clk(Clock), .clr(Reset));
  Register #(.width(32), .trigger("falling")) R21 (.D(DataInput), .en(F21), .Q(Out21), .clk(Clock), .clr(Reset));
  Register #(.width(32), .trigger("falling")) R26 (.D(DataInput), .en(F26), .Q(Out26), .clk(Clock), .clr(Reset));
  Register #(.width(32), .trigger("falling")) R31 (.D(DataInput), .en(F31), .Q(Out31), .clk(Clock), .clr(Reset));
  Register #(.width(32), .trigger("falling")) R5 (.D(DataInput), .en(F5), .Q(Out5), .clk(Clock), .clr(Reset));
  Register #(.width(32), .trigger("falling")) R12 (.D(DataInput), .en(F12), .Q(Out12), .clk(Clock), .clr(Reset));
  Register #(.width(32), .trigger("falling")) R17 (.D(DataInput), .en(F17), .Q(Out17), .clk(Clock), .clr(Reset));
  Register #(.width(32), .trigger("falling")) R22 (.D(DataInput), .en(F22), .Q(Out22), .clk(Clock), .clr(Reset));
  Register #(.width(32), .trigger("falling")) R27 (.D(DataInput), .en(F27), .Q(Out27), .clk(Clock), .clr(Reset));
  Register #(.width(32), .trigger("falling")) R0 (.D(DataInput), .en(1'b0), .Q(Out0), .clk(Clock), .clr(Reset));
  Register #(.width(32), .trigger("falling")) R6 (.D(DataInput), .en(F6), .Q(Out6), .clk(Clock), .clr(Reset));

  // Other names for the same wires on the sheet: CLK = Clock; DA[4:0] = Data_Addr; DI[31:0] = DataInput;
  //   OutA[31:0] = RegisterA; OutB[31:0] = RegisterB; Rst = Reset; RW = ReadWrite; SA[4:0] = SelectorA;
  //   SB[4:0] = SelectorB

  // Notes on the sheet:
  //   INPUTS
  //   OUTPUTS
  //   DECODER
  //   REGISTERS
endmodule

module HI_LO_Registers (
  input  [31:0] HI_in,
  input  [31:0] Lo_in,
  input  HI_LO_enable,
  input  Reset,
  input  Clock,
  output [31:0] OutputHi,
  output [31:0] OutputLo
);

  Register #(.width(32), .trigger("falling")) RegisterHi (
    .D(HI_in), .en(HI_LO_enable), .Q(OutputHi), .clk(Clock), .clr(Reset));
  Register #(.width(32), .trigger("falling")) RegisterLo (
    .D(Lo_in), .en(HI_LO_enable), .Q(OutputLo), .clk(Clock), .clr(Reset));

  // Other names for the same wires on the sheet: CLK = Clock; Hi[31:0] = HI_in; HI_LO_EN = HI_LO_enable;
  //   Lo[31:0] = Lo_in; OutHi[31:0] = OutputHi; OutLo[31:0] = OutputLo; Rst = Reset

  // Notes on the sheet:
  //   INPUTS
  //   OUTPUTS
endmodule
